// Logisim project 1-CRC.circ as structural Verilog: 3 circuits, main circuit main
module main (
  output [10:0] out_1,
  output out_2
);

  wire clock_1_out;
  wire [7:0] counter_1_q;
  wire [11:0] rom_1_data;

  Counter counter_1 (.Q(counter_1_q), .carry(out_2), .clk(clock_1_out));  // open: load, D, count, clr
  Clock clock_1 (.out(clock_1_out));
  ROM #(.dataWidth(12)) rom_1 (.addr(counter_1_q), .data(rom_1_data));  // open: sel
  CRC crc_1 (.A(rom_1_data[7:0]), .B(rom_1_data[11:8]), .C(out_1));

  // Notes on the sheet:
  //   contents of rom_1 (hex, n*v repeats v):
  //   bca c8e 800
endmodule

module CRC (
  input  [7:0] A,
  input  [3:0] B,
  output [10:0] C
);

  wire [2:0] n4_bit_div_1_c, n4_bit_div_2_c, n4_bit_div_3_c, n4_bit_div_4_c;

  _4_bit_div u_4_bit_div_1 (.A(A[7:4]), .B(B), .C(n4_bit_div_1_c));  // open: D
  _4_bit_div u_4_bit_div_2 (.A({n4_bit_div_1_c, A[3]}), .B(B), .C(n4_bit_div_2_c));  // open: D
  _4_bit_div u_4_bit_div_3 (.A({n4_bit_div_2_c, A[2]}), .B(B), .C(n4_bit_div_3_c));  // open: D
  _4_bit_div u_4_bit_div_4 (.A({n4_bit_div_3_c, A[1]}), .B(B), .C(n4_bit_div_4_c));  // open: D
  _4_bit_div u_4_bit_div_5 (.A({n4_bit_div_4_c, A[0]}), .B(B), .C(C[2:0]));  // open: D

  assign C[10:3] = A;
endmodule

module _4_bit_div (
  input  [3:0] A,
  input  [3:0] B,
  output [2:0] C,
  output D
);

  wire [2:0] demultiplexer_1_out0, demultiplexer_1_out1, xor_1_out;

  Demultiplexer #(.width(3)) demultiplexer_1 (
    .out0(demultiplexer_1_out0), .out1(demultiplexer_1_out1), .in(A[2:0]), .sel(A[3]));  // open: en
  assign xor_1_out = demultiplexer_1_out1 ^ B[2:0];  // XOR_Gate xor_1, 3 bits wide
  Multiplexer #(.width(3)) multiplexer_1 (
    .in0(demultiplexer_1_out0), .in1(xor_1_out), .out(C), .sel(A[3]));  // open: en

  assign D = A[3];
endmodule
