// Logisim project 2-alu.circ as structural Verilog: 4 circuits, main circuit main
module main (
);

  alu alu_1 ();  // open: A, B, ALUOp, C
endmodule

module alu (
  input  [3:0] A,
  input  [3:0] B,
  input  [1:0] ALUOp,
  output [3:0] C
);

  wire [3:0] and_1_out, demultiplexer_1_out0, demultiplexer_1_out1, multiplexer_1_out, n4bit_add_1_sum,
       not_1_out, or_1_out;

  Multiplexer #(.width(4)) multiplexer_1 (
    .in0(B), .in1(not_1_out), .out(multiplexer_1_out), .sel(ALUOp[0]));  // open: en
  assign not_1_out = ~B;  // NOT_Gate not_1, 4 bits wide
  _4bit_add u_4bit_add_1 (.a(A), .b(multiplexer_1_out), .ci(ALUOp[0]), .sum(n4bit_add_1_sum));  // open: co
  assign and_1_out = A & B;  // AND_Gate and_1, 4 bits wide
  assign or_1_out = A | B;  // OR_Gate or_1, 4 bits wide
  Demultiplexer #(.width(4)) demultiplexer_1 (
    .out0(demultiplexer_1_out0), .out1(demultiplexer_1_out1), .in(n4bit_add_1_sum), .sel(ALUOp[0]));  // open: en
  Multiplexer #(.select(2), .width(4)) multiplexer_2 (
    .in0(demultiplexer_1_out0), .in1(demultiplexer_1_out1), .in2(and_1_out), .in3(or_1_out), .out(C),
    .sel(ALUOp));  // open: en
endmodule

module _4bit_add (
  input  [3:0] a,
  input  [3:0] b,
  input  ci,
  output co,
  output [3:0] sum
);

  wire n1bit_add_1_co, n1bit_add_2_co, n1bit_add_3_co;

  _1bit_add u_1bit_add_1 (.a(a[0]), .b(b[0]), .ci(ci), .co(n1bit_add_1_co), .s(sum[0]));
  _1bit_add u_1bit_add_2 (.a(a[1]), .b(b[1]), .ci(n1bit_add_1_co), .co(n1bit_add_2_co), .s(sum[1]));
  _1bit_add u_1bit_add_3 (.a(a[2]), .b(b[2]), .ci(n1bit_add_2_co), .co(n1bit_add_3_co), .s(sum[2]));
  _1bit_add u_1bit_add_4 (.a(a[3]), .b(b[3]), .ci(n1bit_add_3_co), .co(co), .s(sum[3]));
endmodule

module _1bit_add (
  input  a,
  input  b,
  input  ci,
  output co,
  output s
);

  wire and_1_out, and_2_out, and_3_out, and_4_out, and_5_out, and_6_out, and_7_out, not_1_out, not_2_out,
       not_3_out, not_4_out, not_5_out, not_6_out;

  and and_1 (and_1_out, b, ci);
  and and_2 (and_2_out, a, ci);
  and and_3 (and_3_out, a, b);
  not not_1 (not_1_out, a);
  not not_2 (not_2_out, b);
  not not_3 (not_3_out, a);
  not not_4 (not_4_out, ci);
  not not_5 (not_5_out, b);
  not not_6 (not_6_out, ci);
  or or_1 (co, and_1_out, and_2_out, and_3_out);
  and and_4 (and_4_out, not_1_out, not_2_out, ci);
  and and_5 (and_5_out, not_3_out, b, not_4_out);
  and and_6 (and_6_out, a, not_5_out, not_6_out);
  and and_7 (and_7_out, a, b, ci);
  or or_2 (s, and_4_out, and_5_out, and_6_out, and_7_out);
endmodule
