// Logisim project 3-fsm.circ as structural Verilog: 7 circuits, main circuit main
module main (
  output out,
  output out_2
);

  wire clock_1_out;
  wire [2:0] rom_1_data;
  wire [7:0] counter_1_q;

  Counter counter_1 (.Q(counter_1_q), .carry(out_2), .clk(clock_1_out));  // open: load, D, count, clr
  Clock clock_1 (.out(clock_1_out));
  ROM #(.dataWidth(3)) rom_1 (.addr(counter_1_q), .data(rom_1_data));  // open: sel
  try_4 try_4_1 (.CLR(rom_1_data[0]), .In(rom_1_data[2:1]), .Z(out));

  // Notes on the sheet:
  //   contents of rom_1 (hex, n*v repeats v):
  //   6 2 0 4 2 4 4 2 2 0 0 2 2 4 4 0 2 6 4 2 0 5 3 2 4
endmodule

module fsm (
  input  CLR,
  input  [1:0] In,
  output Z
);

  wire and_1_out, and_2_out, and_3_out, and_4_out, and_5_out, clock_1_out, clock_2_out, not_1_out, not_2_out,
       not_3_out, not_4_out, not_5_out, not_6_out, not_7_out, not_8_out, not_9_out, or_1_out, or_2_out,
       register_1_q, register_2_q;
  wire [1:0] multiplexer_1_out;

  Clock clock_1 (.out(clock_1_out));
  and and_1 (and_1_out, CLR, clock_1_out);
  Multiplexer #(.width(2)) multiplexer_1 (.in0(In), .in1(2'b00), .out(multiplexer_1_out), .sel(CLR));  // open: en
  not not_1 (not_1_out, register_1_q);
  not not_2 (not_2_out, multiplexer_1_out[0]);
  not not_3 (not_3_out, register_2_q);
  not not_4 (not_4_out, multiplexer_1_out[0]);
  not not_5 (not_5_out, multiplexer_1_out[1]);
  not not_6 (not_6_out, register_2_q);
  not not_7 (not_7_out, multiplexer_1_out[0]);
  not not_8 (not_8_out, register_2_q);
  not not_9 (not_9_out, multiplexer_1_out[0]);
  and and_2 (and_2_out, not_1_out, register_2_q, not_2_out);
  and and_3 (and_3_out, register_1_q, not_3_out, not_4_out);
  and and_4 (and_4_out, not_5_out, multiplexer_1_out[0]);
  and and_5 (and_5_out, register_1_q, not_6_out, not_7_out);
  and and_6 (Z, register_1_q, not_8_out, not_9_out);
  or or_1 (or_1_out, and_2_out, and_3_out);
  or or_2 (or_2_out, and_4_out, and_5_out);
  Register #(.width(1)) register_1 (.D(or_1_out), .en(1'b1), .Q(register_1_q), .clk(clock_2_out), .clr(and_1_out));
  Register #(.width(1)) register_2 (.D(or_2_out), .en(1'b1), .Q(register_2_q), .clk(clock_2_out), .clr(and_1_out));
  Clock clock_2 (.out(clock_2_out));
endmodule

module try (
  input  CLR,
  input  [1:0] In,
  output Z
);

  wire a1, a2, a3, a4, and_1_out, and_2_out, and_3_out, and_4_out, and_5_out, and_6_out, and_7_out,
       and_8_out, and_9_out, and_10_out, and_11_out, and_12_out, and_13_out, clock_1_out, not_1_out,
       not_2_out, not_3_out, not_4_out, not_5_out, not_6_out, not_7_out, not_8_out, not_9_out, not_10_out,
       not_11_out, not_12_out, not_13_out, not_14_out, not_15_out, not_16_out, not_17_out, not_18_out,
       not_19_out, not_20_out, not_21_out, not_22_out, not_23_out, not_24_out, not_25_out, not_26_out,
       not_27_out, not_28_out, not_29_out, not_30_out, not_31_out, not_32_out, or_1_out, or_2_out, or_3_out,
       or_4_out;
  wire [1:0] multiplexer_1_out;

  Multiplexer #(.width(2)) multiplexer_1 (.in0(In), .in1(2'b00), .out(multiplexer_1_out), .sel(CLR));  // open: en
  not not_1 (not_1_out, a2);
  not not_2 (not_2_out, a1);
  not not_3 (not_3_out, multiplexer_1_out[0]);
  not not_4 (not_4_out, a1);
  not not_5 (not_5_out, multiplexer_1_out[1]);
  not not_6 (not_6_out, multiplexer_1_out[0]);
  not not_7 (not_7_out, multiplexer_1_out[0]);
  not not_8 (not_8_out, a4);
  not not_9 (not_9_out, a3);
  not not_10 (not_10_out, multiplexer_1_out[0]);
  not not_11 (not_11_out, a4);
  not not_12 (not_12_out, a3);
  not not_13 (not_13_out, multiplexer_1_out[1]);
  not not_14 (not_14_out, multiplexer_1_out[0]);
  not not_15 (not_15_out, a4);
  not not_16 (not_16_out, a3);
  not not_17 (not_17_out, multiplexer_1_out[1]);
  not not_18 (not_18_out, multiplexer_1_out[0]);
  not not_19 (not_19_out, multiplexer_1_out[1]);
  not not_20 (not_20_out, a4);
  not not_21 (not_21_out, a1);
  not not_22 (not_22_out, multiplexer_1_out[1]);
  not not_23 (not_23_out, a3);
  not not_24 (not_24_out, multiplexer_1_out[0]);
  not not_25 (not_25_out, a4);
  not not_26 (not_26_out, a1);
  not not_27 (not_27_out, multiplexer_1_out[1]);
  not not_28 (not_28_out, multiplexer_1_out[0]);
  not not_29 (not_29_out, a2);
  not not_30 (not_30_out, a1);
  not not_31 (not_31_out, multiplexer_1_out[0]);
  not not_32 (not_32_out, multiplexer_1_out[0]);
  and and_1 (and_1_out, a3, not_1_out, not_2_out, multiplexer_1_out[1], not_3_out);
  and and_2 (and_2_out, a3, a2, not_4_out, not_5_out, not_6_out);
  and and_3 (and_3_out, a3, a2, a1, multiplexer_1_out[1], not_7_out);
  and and_4 (and_4_out, not_8_out, not_9_out, a1, multiplexer_1_out[1], not_10_out);
  and and_5 (and_5_out, not_11_out, not_12_out, a2, not_13_out, not_14_out);
  and and_6 (and_6_out, not_15_out, not_16_out, a1, not_17_out);
  and and_7 (and_7_out, a2, a1, multiplexer_1_out[1], not_18_out);
  and and_8 (and_8_out, not_19_out, multiplexer_1_out[0]);
  and and_9 (and_9_out, not_20_out, a2, not_21_out, not_22_out);
  and and_10 (and_10_out, not_23_out, a2, a1, multiplexer_1_out[1], not_24_out);
  and and_11 (and_11_out, not_25_out, a2, not_26_out, not_27_out, not_28_out);
  and and_12 (and_12_out, a3, not_29_out, not_30_out, multiplexer_1_out[1], not_31_out);
  and and_13 (and_13_out, a3, a2, a1, multiplexer_1_out[1], not_32_out);
  or or_1 (or_1_out, and_1_out, and_2_out, and_3_out);
  or or_2 (or_2_out, and_4_out, and_5_out);
  or or_3 (or_3_out, and_6_out, and_7_out);
  or or_4 (or_4_out, and_8_out, and_9_out, and_10_out);
  or or_5 (Z, and_11_out, and_12_out, and_13_out);
  Register #(.width(1)) b4 (.D(or_1_out), .en(1'b1), .Q(a4), .clk(clock_1_out), .clr(CLR));
  Register #(.width(1)) b3 (.D(or_2_out), .en(1'b1), .Q(a3), .clk(clock_1_out), .clr(CLR));
  Register #(.width(1)) b2 (.D(or_3_out), .en(1'b1), .Q(a2), .clk(clock_1_out), .clr(CLR));
  Register #(.width(1)) b1 (.D(or_4_out), .en(1'b1), .Q(a1), .clk(clock_1_out), .clr(CLR));
  Clock clock_1 (.out(clock_1_out));

  // Other names for the same wires on the sheet: rst = CLR
endmodule

module try_2 (
  input  CLR,
  input  [1:0] In,
  output Z
);

  wire a1, a2, a3, and_1_out, and_2_out, and_3_out, and_4_out, and_5_out, and_6_out, and_7_out, and_8_out,
       clock_1_out, not_1_out, not_2_out, not_3_out, not_4_out, not_5_out, not_6_out, not_7_out, not_8_out,
       not_9_out, not_10_out, not_11_out, not_12_out, not_13_out, or_1_out, or_2_out, or_3_out;

  not not_1 (not_1_out, a3);
  not not_2 (not_2_out, In[0]);
  not not_3 (not_3_out, In[0]);
  not not_4 (not_4_out, a2);
  not not_5 (not_5_out, In[0]);
  not not_6 (not_6_out, a3);
  not not_7 (not_7_out, In[1]);
  not not_8 (not_8_out, In[1]);
  not not_9 (not_9_out, In[0]);
  not not_10 (not_10_out, a3);
  not not_11 (not_11_out, a1);
  not not_12 (not_12_out, In[0]);
  not not_13 (not_13_out, In[0]);
  and and_1 (and_1_out, not_1_out, a2, not_2_out);
  and and_2 (and_2_out, a3, a1, not_3_out);
  and and_3 (and_3_out, not_4_out, a1, not_5_out);
  and and_4 (and_4_out, not_6_out, a1, not_7_out, In[0]);
  and and_5 (and_5_out, not_8_out, In[0]);
  and and_6 (and_6_out, a2, a1, not_9_out);
  and and_7 (and_7_out, not_10_out, a2, not_11_out, not_12_out);
  and and_8 (and_8_out, a3, a1, not_13_out);
  or or_1 (or_1_out, and_1_out, and_2_out);
  or or_2 (or_2_out, and_3_out, and_4_out);
  or or_3 (or_3_out, and_5_out, and_6_out);
  or or_4 (Z, and_7_out, and_8_out);
  Register #(.width(1)) register_1 (.D(or_1_out), .en(1'b1), .Q(a3), .clk(clock_1_out), .clr(CLR));
  Register #(.width(1)) register_2 (.D(or_2_out), .en(1'b1), .Q(a2), .clk(clock_1_out), .clr(CLR));
  Register #(.width(1)) register_3 (.D(or_3_out), .en(1'b1), .Q(a1), .clk(clock_1_out), .clr(CLR));
  Clock clock_1 (.out(clock_1_out));
endmodule

module debug (
  input  A3,
  input  A2,
  input  A1,
  input  in1,
  input  in0,
  output b3,
  output b2,
  output b1,
  output out
);

  wire and_1_out, and_2_out, and_3_out, and_4_out, and_5_out, and_6_out, and_7_out, and_8_out, not_1_out,
       not_2_out, not_3_out, not_4_out, not_5_out, not_6_out, not_7_out, not_8_out, not_9_out, not_10_out,
       not_11_out, not_12_out, not_13_out;

  not not_1 (not_1_out, A3);
  not not_2 (not_2_out, in0);
  not not_3 (not_3_out, in0);
  not not_4 (not_4_out, A2);
  not not_5 (not_5_out, in0);
  not not_6 (not_6_out, A3);
  not not_7 (not_7_out, in1);
  not not_8 (not_8_out, in1);
  not not_9 (not_9_out, in0);
  not not_10 (not_10_out, A3);
  not not_11 (not_11_out, A1);
  not not_12 (not_12_out, in0);
  not not_13 (not_13_out, in0);
  and and_1 (and_1_out, not_1_out, A2, not_2_out);
  and and_2 (and_2_out, A3, A1, not_3_out);
  and and_3 (and_3_out, not_4_out, A1, not_5_out);
  and and_4 (and_4_out, not_6_out, A1, not_7_out, in0);
  and and_5 (and_5_out, not_8_out, in0);
  and and_6 (and_6_out, A2, A1, not_9_out);
  and and_7 (and_7_out, not_10_out, A2, not_11_out, not_12_out);
  and and_8 (and_8_out, A3, A1, not_13_out);
  or or_1 (b3, and_1_out, and_2_out);
  or or_2 (b2, and_3_out, and_4_out);
  or or_3 (b1, and_5_out, and_6_out);
  or or_4 (out, and_7_out, and_8_out);
endmodule

module try_3 (
  input  CLR,
  input  [1:0] In,
  output Z
);

  wire and_1_out, and_2_out, and_3_out, and_4_out, clock_1_out, not_1_out, not_2_out, not_3_out, not_4_out,
       not_5_out, not_6_out, not_7_out, not_8_out, not_9_out, or_1_out, or_2_out, register_1_q, register_2_q;

  not not_1 (not_1_out, register_1_q);
  not not_2 (not_2_out, In[0]);
  not not_3 (not_3_out, register_2_q);
  not not_4 (not_4_out, In[0]);
  not not_5 (not_5_out, In[1]);
  not not_6 (not_6_out, register_2_q);
  not not_7 (not_7_out, In[0]);
  not not_8 (not_8_out, register_2_q);
  not not_9 (not_9_out, In[0]);
  and and_1 (and_1_out, not_1_out, register_2_q, not_2_out);
  and and_2 (and_2_out, register_1_q, not_3_out, not_4_out);
  and and_3 (and_3_out, not_5_out, In[0]);
  and and_4 (and_4_out, register_1_q, not_6_out, not_7_out);
  and and_5 (Z, register_1_q, not_8_out, not_9_out);
  or or_1 (or_1_out, and_1_out, and_2_out);
  or or_2 (or_2_out, and_3_out, and_4_out);
  Register #(.width(1)) register_1 (.D(or_1_out), .en(1'b1), .Q(register_1_q), .clk(clock_1_out), .clr(CLR));
  Register #(.width(1)) register_2 (.D(or_2_out), .en(1'b1), .Q(register_2_q), .clk(clock_1_out), .clr(CLR));
  Clock clock_1 (.out(clock_1_out));
endmodule

module try_4 (
  input  CLR,
  input  [1:0] In,
  output Z
);

  wire and_1_out, and_2_out, and_3_out, and_4_out, and_5_out, clock_1_out, clock_2_out, not_1_out, not_2_out,
       not_3_out, not_4_out, not_5_out, not_6_out, not_7_out, not_8_out, not_9_out, or_1_out, or_2_out,
       register_1_q, register_2_q;
  wire [1:0] multiplexer_1_out;

  Clock clock_1 (.out(clock_1_out));
  and and_1 (and_1_out, CLR, clock_1_out);
  Multiplexer #(.width(2)) multiplexer_1 (.in0(In), .in1(2'b00), .out(multiplexer_1_out), .sel(CLR));  // open: en
  not not_1 (not_1_out, register_1_q);
  not not_2 (not_2_out, multiplexer_1_out[0]);
  not not_3 (not_3_out, register_2_q);
  not not_4 (not_4_out, multiplexer_1_out[0]);
  not not_5 (not_5_out, multiplexer_1_out[1]);
  not not_6 (not_6_out, register_2_q);
  not not_7 (not_7_out, multiplexer_1_out[0]);
  not not_8 (not_8_out, register_2_q);
  not not_9 (not_9_out, multiplexer_1_out[0]);
  and and_2 (and_2_out, not_1_out, register_2_q, not_2_out);
  and and_3 (and_3_out, register_1_q, not_3_out, not_4_out);
  and and_4 (and_4_out, not_5_out, multiplexer_1_out[0]);
  and and_5 (and_5_out, register_1_q, not_6_out, not_7_out);
  and and_6 (Z, register_1_q, not_8_out, not_9_out);
  or or_1 (or_1_out, and_2_out, and_3_out);
  or or_2 (or_2_out, and_4_out, and_5_out);
  Register #(.width(1)) register_1 (.D(or_1_out), .en(1'b1), .Q(register_1_q), .clk(clock_2_out), .clr(and_1_out));
  Register #(.width(1)) register_2 (.D(or_2_out), .en(1'b1), .Q(register_2_q), .clk(clock_2_out), .clr(and_1_out));
  Clock clock_2 (.out(clock_2_out));
endmodule
