// Logisim project 4-fsm_modify.circ as structural Verilog: 2 circuits, main circuit main
module main (
);

  fsm fsm_1 ();  // open: CLR, In, Z
endmodule

module fsm (
  input  CLR,
  input  [1:0] In,
  output Z
);

  wire and_1_out, and_2_out, and_3_out, and_4_out, clock_1_out, clock_2_out, multiplexer_2_out, not_1_out,
       not_2_out, not_3_out, not_4_out, not_5_out, not_6_out, not_7_out, not_8_out, not_9_out, or_1_out,
       or_2_out, register_1_q, register_2_q, register_3_q;
  wire [1:0] multiplexer_1_out;

  Register #(.width(1)) register_1 (.D(CLR), .Q(register_1_q), .clk(clock_1_out));  // open: en, clr
  Clock clock_1 (.out(clock_1_out));
  Multiplexer #(.width(2)) multiplexer_1 (.in0(In), .in1(2'b00), .out(multiplexer_1_out), .sel(CLR));  // open: en
  Multiplexer multiplexer_2 (.in0(1'b0), .in1(register_1_q), .out(multiplexer_2_out), .sel(CLR));  // open: en
  not not_1 (not_1_out, register_2_q);
  not not_2 (not_2_out, multiplexer_1_out[0]);
  not not_3 (not_3_out, register_3_q);
  not not_4 (not_4_out, multiplexer_1_out[0]);
  not not_5 (not_5_out, multiplexer_1_out[1]);
  not not_6 (not_6_out, register_3_q);
  not not_7 (not_7_out, multiplexer_1_out[0]);
  not not_8 (not_8_out, register_3_q);
  not not_9 (not_9_out, multiplexer_1_out[0]);
  and and_1 (and_1_out, not_1_out, register_3_q, not_2_out);
  and and_2 (and_2_out, register_2_q, not_3_out, not_4_out);
  and and_3 (and_3_out, not_5_out, multiplexer_1_out[0]);
  and and_4 (and_4_out, register_2_q, not_6_out, not_7_out);
  and and_5 (Z, register_2_q, not_8_out, not_9_out);
  or or_1 (or_1_out, and_1_out, and_2_out);
  or or_2 (or_2_out, and_3_out, and_4_out);
  Register #(.width(1)) register_2 (
    .D(or_1_out), .en(1'b1), .Q(register_2_q), .clk(clock_2_out), .clr(multiplexer_2_out));
  Register #(.width(1)) register_3 (
    .D(or_2_out), .en(1'b1), .Q(register_3_q), .clk(clock_2_out), .clr(multiplexer_2_out));
  Clock clock_2 (.out(clock_2_out));
endmodule
