// Logisim project P0.L0.Q3_FSM.circ as structural Verilog: 1 circuit, main circuit fsm
module fsm (
  input  CLR,
  input  [1:0] In,
  output out_3
);

  wire clock_1_out;
  wire [1:0] multiplexer_1_out, register_1_q, rom_1_data;

  ROM #(.addrWidth(4), .dataWidth(2)) rom_1 (.addr({register_1_q, In}), .data(rom_1_data));  // open: sel
  Multiplexer #(.width(2), .enable("false")) multiplexer_1 (
    .in0(rom_1_data), .in1(2'b00), .out(multiplexer_1_out), .sel(CLR));
  Register #(.width(2)) register_1 (.D(multiplexer_1_out), .Q(register_1_q), .clk(clock_1_out));  // open: en, clr
  Clock clock_1 (.out(clock_1_out));
  ROM #(.addrWidth(4), .dataWidth(1)) rom_2 (.addr({register_1_q, In}), .data(out_3));  // open: sel

  // Notes on the sheet:
  //   contents of rom_1 (hex, n*v repeats v):
  //   0 1 0 0 2 1 2 0 3 1 3 0 0 1
  //   contents of rom_2 (hex, n*v repeats v):
  //   8*0 1 0 1
endmodule
