// Logisim project ALU.circ as structural Verilog: 3 circuits, main circuit add
module add (
  input  ci,
  input  [3:0] a,
  input  [3:0] b,
  output [3:0] s0,
  output c0
);

  wire add1_1_c0, add1_2_c0, add1_3_c0;

  add1 add1_1 (.a(a[0]), .b(b[0]), .ci(ci), .c0(add1_1_c0), .s0(s0[0]));
  add1 add1_2 (.a(a[1]), .b(b[1]), .ci(add1_1_c0), .c0(add1_2_c0), .s0(s0[1]));
  add1 add1_3 (.a(a[2]), .b(b[2]), .ci(add1_2_c0), .c0(add1_3_c0), .s0(s0[2]));
  add1 add1_4 (.a(a[3]), .b(b[3]), .ci(add1_3_c0), .c0(c0), .s0(s0[3]));
endmodule

module alu (
  input  [3:0] A,
  input  [3:0] B,
  input  [1:0] ALUOp,
  output [3:0] C
);

  wire [3:0] add_1_s0, and_1_out, demultiplexer_1_out0, demultiplexer_1_out1, multiplexer_1_out, not_1_out,
       or_1_out;

  assign not_1_out = ~B;  // NOT_Gate not_1, 4 bits wide
  Multiplexer #(.width(4)) multiplexer_1 (
    .in0(B), .in1(not_1_out), .out(multiplexer_1_out), .sel(ALUOp[0]));  // open: en
  add add_1 (.ci(ALUOp[0]), .a(A), .b(multiplexer_1_out), .s0(add_1_s0));  // open: c0
  assign and_1_out = A & B;  // AND_Gate and_1, 4 bits wide
  assign or_1_out = A | B;  // OR_Gate or_1, 4 bits wide
  Demultiplexer #(.width(4)) demultiplexer_1 (
    .out0(demultiplexer_1_out0), .out1(demultiplexer_1_out1), .in(add_1_s0), .sel(ALUOp[0]));  // open: en
  Multiplexer #(.select(2), .width(4)) multiplexer_2 (
    .in0(demultiplexer_1_out0), .in1(demultiplexer_1_out1), .in2(and_1_out), .in3(or_1_out), .out(C),
    .sel(ALUOp));  // open: en
endmodule

module add1 (
  input  a,
  input  b,
  input  ci,
  output c0,
  output s0
);

  wire and_1_out, and_2_out, and_3_out, and_4_out, and_5_out, and_6_out, and_7_out, not_1_out, not_2_out,
       not_3_out, not_4_out, not_5_out, not_6_out;

  and and_1 (and_1_out, b, ci);
  and and_2 (and_2_out, a, ci);
  and and_3 (and_3_out, a, b);
  not not_1 (not_1_out, a);
  not not_2 (not_2_out, b);
  not not_3 (not_3_out, a);
  not not_4 (not_4_out, ci);
  not not_5 (not_5_out, b);
  not not_6 (not_6_out, ci);
  or or_1 (c0, and_1_out, and_2_out, and_3_out);
  and and_4 (and_4_out, not_1_out, not_2_out, ci);
  and and_5 (and_5_out, not_3_out, b, not_4_out);
  and and_6 (and_6_out, a, not_5_out, not_6_out);
  and and_7 (and_7_out, a, b, ci);
  or or_2 (s0, and_4_out, and_5_out, and_6_out, and_7_out);
endmodule
