// Logisim project Comparator.circ as structural Verilog: 3 circuits, main circuit main
module main (
  input  [3:0] A,
  input  [3:0] B,
  output Out
);

  wire and_1_out, and_2_out, and_3_out, n1_comp_1_eq, n1_comp_1_out, n1_comp_2_eq, n1_comp_2_out,
       n1_comp_3_eq, n1_comp_3_out, n1_comp_4_out, not_1_out, not_2_out;

  _1_comp u_1_comp_1 (.A(A[3]), .B(B[3]), .OUT(n1_comp_1_out), .eq(n1_comp_1_eq));
  and and_1 (and_1_out, n1_comp_1_eq, n1_comp_2_out);
  _1_comp u_1_comp_2 (.A(A[2]), .B(B[2]), .OUT(n1_comp_2_out), .eq(n1_comp_2_eq));
  _1_comp u_1_comp_3 (.A(A[1]), .B(B[1]), .OUT(n1_comp_3_out), .eq(n1_comp_3_eq));
  _1_comp u_1_comp_4 (.A(A[0]), .B(B[0]), .OUT(n1_comp_4_out));  // open: eq
  not not_1 (not_1_out, and_1_out);
  and and_2 (and_2_out, not_1_out, n1_comp_2_eq, n1_comp_3_out);
  not not_2 (not_2_out, and_2_out);
  and and_3 (and_3_out, not_2_out, n1_comp_3_eq, n1_comp_4_out);
  or or_1 (Out, n1_comp_1_out, and_1_out, and_2_out, and_3_out);
endmodule

module _1_comp (
  input  A,
  input  B,
  output OUT,
  output eq
);

  wire and_2_out, and_3_out, not_1_out, not_2_out, not_3_out;

  not not_1 (not_1_out, B);
  not not_2 (not_2_out, A);
  not not_3 (not_3_out, B);
  and and_1 (OUT, A, not_1_out);
  and and_2 (and_2_out, not_2_out, not_3_out);
  and and_3 (and_3_out, A, B);
  or or_1 (eq, and_2_out, and_3_out);
endmodule

module comparator (
  input  [3:0] A,
  input  [3:0] B,
  output Out
);

  wire and_1_out, and_2_out, and_3_out, n1_comp_1_eq, n1_comp_1_out, n1_comp_2_eq, n1_comp_2_out,
       n1_comp_3_eq, n1_comp_3_out, n1_comp_4_out, not_1_out, not_2_out;

  _1_comp u_1_comp_1 (.A(A[3]), .B(B[3]), .OUT(n1_comp_1_out), .eq(n1_comp_1_eq));
  and and_1 (and_1_out, n1_comp_1_eq, n1_comp_2_out);
  _1_comp u_1_comp_2 (.A(A[2]), .B(B[2]), .OUT(n1_comp_2_out), .eq(n1_comp_2_eq));
  _1_comp u_1_comp_3 (.A(A[1]), .B(B[1]), .OUT(n1_comp_3_out), .eq(n1_comp_3_eq));
  _1_comp u_1_comp_4 (.A(A[0]), .B(B[0]), .OUT(n1_comp_4_out));  // open: eq
  not not_1 (not_1_out, and_1_out);
  and and_2 (and_2_out, not_1_out, n1_comp_2_eq, n1_comp_3_out);
  not not_2 (not_2_out, and_2_out);
  and and_3 (and_3_out, not_2_out, n1_comp_3_eq, n1_comp_4_out);
  or or_1 (Out, n1_comp_1_out, and_1_out, and_2_out, and_3_out);
endmodule
