// Logisim project Signed_Comparator.circ as structural Verilog: 2 circuits, main circuit 1_comp
module _1_comp (
  input  A,
  input  B,
  output OUT,
  output eq
);

  wire and_2_out, and_3_out, not_1_out, not_2_out, not_3_out;

  not not_1 (not_1_out, B);
  not not_2 (not_2_out, A);
  not not_3 (not_3_out, B);
  and and_1 (OUT, A, not_1_out);
  and and_2 (and_2_out, not_2_out, not_3_out);
  and and_3 (and_3_out, A, B);
  or or_1 (eq, and_2_out, and_3_out);
endmodule

module comparator (
  input  [3:0] A,
  input  [3:0] B,
  output out_3
);

  wire a0, a1, a2, and_1_out, and_2_out, b0, b1, b2, n1_comp_1_eq, n1_comp_1_out, n1_comp_2_eq,
       n1_comp_2_out, n1_comp_3_out, not_1_out, not_2_out, not_3_out, not_4_out, not_5_out, not_6_out,
       or_1_out;

  not not_1 (not_1_out, A[0]);
  not not_2 (not_2_out, A[1]);
  not not_3 (not_3_out, A[2]);
  not not_4 (not_4_out, B[0]);
  not not_5 (not_5_out, B[1]);
  not not_6 (not_6_out, B[2]);
  Multiplexer multiplexer_1 (.in0(A[0]), .in1(not_1_out), .out(a0), .sel(A[3]));  // open: en
  Multiplexer multiplexer_2 (.in0(A[1]), .in1(not_2_out), .out(a1), .sel(A[3]));  // open: en
  Multiplexer multiplexer_3 (.in0(A[2]), .in1(not_3_out), .out(a2), .sel(A[3]));  // open: en
  Multiplexer multiplexer_4 (.in0(B[0]), .in1(not_4_out), .out(b0), .sel(B[3]));  // open: en
  Multiplexer multiplexer_5 (.in0(B[1]), .in1(not_5_out), .out(b1), .sel(B[3]));  // open: en
  Multiplexer multiplexer_6 (.in0(B[2]), .in1(not_6_out), .out(b2), .sel(B[3]));  // open: en
  _1_comp u_1_comp_1 (.A(a2), .B(b2), .OUT(n1_comp_1_out), .eq(n1_comp_1_eq));
  _1_comp u_1_comp_2 (.A(a1), .B(b1), .OUT(n1_comp_2_out), .eq(n1_comp_2_eq));
  _1_comp u_1_comp_3 (.A(a0), .B(b0), .OUT(n1_comp_3_out));  // open: eq
  and and_1 (and_1_out, n1_comp_1_eq, n1_comp_2_out);
  and and_2 (and_2_out, n1_comp_2_eq, n1_comp_3_out);
  or or_1 (or_1_out, n1_comp_1_out, and_1_out, and_2_out);
  Multiplexer #(.select(2)) multiplexer_7 (
    .in0(or_1_out), .in1(1'b0), .in2(1'b1), .in3(or_1_out), .out(out_3), .sel({B[3], A[3]}));  // open: en
endmodule
