// Logisim project GPR.circ as structural Verilog
module gpr (
  input  [31:0] in_1,
  input  [31:0] in_2,
  input  in_3
);

  wire clk, WE;
  wire [31:0] _0, _1, _2, _3, _4, _5, _6, _7, _8, _9, _10, _11, _12, _13, _14, _15, _16, _17, _18, _19, _20,
       _21, _22, _23, _24, _25, _26, _27, _28, _29, _30, _31;

  Clock clock_1 (.out(clk));
  Register #(.width(32)) register_1 (.D(in_1), .en(WE), .Q(_0), .clk(clk), .clr(in_3));
  Register #(.width(32)) register_2 (.D(in_1), .en(WE), .Q(_4), .clk(clk), .clr(in_3));
  Register #(.width(32)) register_3 (.D(in_1), .en(WE), .Q(_8), .clk(clk), .clr(in_3));
  Register #(.width(32)) register_4 (.D(in_1), .en(WE), .Q(_12), .clk(clk), .clr(in_3));
  Register #(.width(32)) register_5 (.D(in_1), .en(WE), .Q(_16), .clk(clk), .clr(in_3));
  Register #(.width(32)) register_6 (.D(in_1), .en(WE), .Q(_20), .clk(clk), .clr(in_3));
  Register #(.width(32)) register_7 (.D(in_1), .en(WE), .Q(_24), .clk(clk), .clr(in_3));
  Register #(.width(32)) register_8 (.D(in_1), .en(WE), .Q(_28), .clk(clk), .clr(in_3));
  Register #(.width(32)) register_9 (.D(in_1), .en(WE), .Q(_1), .clk(clk), .clr(in_3));
  Register #(.width(32)) register_10 (.D(in_1), .en(WE), .Q(_5), .clk(clk), .clr(in_3));
  Register #(.width(32)) register_11 (.D(in_1), .en(WE), .Q(_9), .clk(clk), .clr(in_3));
  Register #(.width(32)) register_12 (.D(in_1), .en(WE), .Q(_13), .clk(clk), .clr(in_3));
  Register #(.width(32)) register_13 (.D(in_1), .en(WE), .Q(_17), .clk(clk), .clr(in_3));
  Register #(.width(32)) register_14 (.D(in_1), .en(WE), .Q(_21), .clk(clk), .clr(in_3));
  Register #(.width(32)) register_15 (.D(in_1), .en(WE), .Q(_25), .clk(clk), .clr(in_3));
  Register #(.width(32)) register_16 (.D(in_1), .en(WE), .Q(_29), .clk(clk), .clr(in_3));
  Register #(.width(32)) register_17 (.D(in_1), .en(WE), .Q(_2), .clk(clk), .clr(in_3));
  Register #(.width(32)) register_18 (.D(in_1), .en(WE), .Q(_6), .clk(clk), .clr(in_3));
  Register #(.width(32)) register_19 (.D(in_1), .en(WE), .Q(_10), .clk(clk), .clr(in_3));
  Register #(.width(32)) register_20 (.D(in_1), .en(WE), .Q(_14), .clk(clk), .clr(in_3));
  Register #(.width(32)) register_21 (.D(in_1), .en(WE), .Q(_18), .clk(clk), .clr(in_3));
  Register #(.width(32)) register_22 (.D(in_1), .en(WE), .Q(_22), .clk(clk), .clr(in_3));
  Register #(.width(32)) register_23 (.D(in_1), .en(WE), .Q(_26), .clk(clk), .clr(in_3));
  Register #(.width(32)) register_24 (.D(in_1), .en(WE), .Q(_30), .clk(clk), .clr(in_3));
  Register #(.width(32)) register_25 (.D(in_1), .en(WE), .Q(_3), .clk(clk), .clr(in_3));
  Register #(.width(32)) register_26 (.D(in_1), .en(WE), .Q(_7), .clk(clk), .clr(in_3));
  Register #(.width(32)) register_27 (.D(in_1), .en(WE), .Q(_11), .clk(clk), .clr(in_3));
  Register #(.width(32)) register_28 (.D(in_1), .en(WE), .Q(_15), .clk(clk), .clr(in_3));
  Register #(.width(32)) register_29 (.D(in_1), .en(WE), .Q(_19), .clk(clk), .clr(in_3));
  Register #(.width(32)) register_30 (.D(in_1), .en(WE), .Q(_23), .clk(clk), .clr(in_3));
  Register #(.width(32)) register_31 (.D(in_1), .en(WE), .Q(_27), .clk(clk), .clr(in_3));
  Register #(.width(32)) register_32 (.D(in_1), .en(WE), .Q(_31), .clk(clk), .clr(in_3));

  // Other names for the same wires on the sheet: data[31:0] = in_1; reset = in_3
endmodule
