// Logisim project Moore_fsm.circ as structural Verilog: 2 circuits, main circuit fsm
module fsm (
  input  X,
  input  Clr,
  output out
);

  wire and_1_out, and_2_out, clock_1_out, not_1_out, not_2_out, or_1_out, register_1_q, register_2_q;

  not not_1 (not_1_out, X);
  not not_2 (not_2_out, register_2_q);
  and and_1 (and_1_out, register_2_q, not_1_out);
  and and_2 (and_2_out, register_1_q, not_2_out, X);
  or or_1 (or_1_out, and_1_out, and_2_out);
  Register #(.width(1)) register_1 (.D(or_1_out), .Q(register_1_q), .clk(clock_1_out), .clr(Clr));  // open: en
  Register #(.width(1)) register_2 (.D(X), .Q(register_2_q), .clk(clock_1_out), .clr(Clr));  // open: en
  Clock clock_1 (.out(clock_1_out));
  and and_3 (out, or_1_out, X);
endmodule

module test (
  output out_1,
  output out_2
);

  wire clock_1_out;
  wire [1:0] rom_1_data;
  wire [7:0] counter_1_q;

  Clock clock_1 (.out(clock_1_out));
  Counter counter_1 (.Q(counter_1_q), .carry(out_2), .clk(clock_1_out));  // open: load, D, count, clr
  ROM #(.dataWidth(2)) rom_1 (.addr(counter_1_q), .data(rom_1_data));  // open: sel
  fsm fsm_1 (.X(rom_1_data[0]), .Clr(rom_1_data[1]), .out(out_1));

  // Notes on the sheet:
  //   contents of rom_1 (hex, n*v repeats v):
  //   1 0 1 0 1 1 1 0 0 0 1 0 1 0 3 2 3
endmodule
