// Logisim project My_CPU_Mono17.circ as structural Verilog: 9 circuits, main circuit main
module main (
  input  Reset,
  output [31:0] out_2,
  output out_3,
  output [4:0] out_4,
  output [31:0] out_5,
  output out_6,
  output [4:0] out_7,
  output [31:0] out_8
);

  wire ALUSrc, Clk, ExtOp, if_beq, if_bltz, if_j, if_jal, if_jr, if_slt, LessZero, LuiOp, MemToReg, RegDst,
       SllWr, zero;
  wire [1:0] ALUOp;
  wire [4:0] multiplexer_1_out;
  wire [31:0] ALUOut, jr_PC, multiplexer_3_out, multiplexer_4_out, multiplexer_5_out, multiplexer_6_out,
       multiplexer_8_out, Offset, PC4, ReadData, SllResult;

  Clock clock_1 (.out(Clk));
  IFU ifu_1 (
    .if_beq(if_beq), .Offset(Offset), .Clk(Clk), .Reset(Reset), .Ins(out_2), .zero(zero), .if_bltz(if_bltz),
    .LessZero(LessZero), .if_j(if_j), .instr_index(out_2[25:0]), .PC4(PC4), .jr_PC(jr_PC), .if_jr(if_jr));
  Multiplexer #(.width(5)) multiplexer_1 (
    .in0(out_2[20:16]), .in1(out_2[15:11]), .out(multiplexer_1_out), .sel(RegDst));  // open: en
  Multiplexer #(.width(5)) multiplexer_2 (
    .in0(multiplexer_1_out), .in1({5{1'b1}}), .out(out_4), .sel(if_jal));  // open: en
  CONTROLLER controller_1 (
    .OpCode(out_2[31:26]), .Func(out_2[5:0]), .ALUSrc(ALUSrc), .MemWrite(out_6), .RegWrite(out_3),
    .if_beq(if_beq), .ExtOp(ExtOp), .LuiOp(LuiOp), .RegDst(RegDst), .ALUOp(ALUOp), .MemToReg(MemToReg),
    .SllWr(SllWr), .if_bltz(if_bltz), .if_j(if_j), .if_jal(if_jal), .if_jr(if_jr), .if_slt(if_slt));
  GPR gpr_1 (
    .WD(out_5), .RW(out_4), .Clk(Clk), .Reset(Reset), .RA(out_2[25:21]), .RB(out_2[20:16]), .WE(out_3),
    .BusA(jr_PC), .BusB(out_8));
  EXT ext_1 (.Imm16(out_2[15:0]), .Ext32(Offset), .ExtOp(ExtOp), .LuiOp(LuiOp));
  Multiplexer #(.width(32)) multiplexer_3 (
    .in0(out_8), .in1(Offset), .out(multiplexer_3_out), .sel(ALUSrc));  // open: en
  Shifter #(.width(32)) shifter_1 (.in(multiplexer_3_out), .\dist (out_2[10:6]), .out(SllResult));
  ALU alu_1 (
    .BusA(jr_PC), .BusB(multiplexer_3_out), .ALUOp(ALUOp), .alu_output({ALUOut[31:7], out_7, ALUOut[1:0]}),
    .zero(zero), .LessZero(LessZero));
  DM dm_1 (.Address(out_7), .WD(out_8), .WE(out_6), .Clk(Clk), .Reset(Reset), .RD(ReadData));
  Multiplexer #(.width(32)) multiplexer_4 (
    .in0({ALUOut[31:7], out_7, ALUOut[1:0]}), .in1(ReadData), .out(multiplexer_4_out), .sel(MemToReg));  // open: en
  Multiplexer #(.width(32)) multiplexer_5 (
    .in0(multiplexer_4_out), .in1(SllResult), .out(multiplexer_5_out), .sel(SllWr));  // open: en
  Multiplexer #(.width(32)) multiplexer_6 (
    .in0(multiplexer_5_out), .in1(PC4), .out(multiplexer_6_out), .sel(if_jal));  // open: en
  Multiplexer #(.width(32)) multiplexer_7 (
    .in0(multiplexer_6_out), .in1(multiplexer_8_out), .out(out_5), .sel(if_slt));  // open: en
  Multiplexer #(.width(32)) multiplexer_8 (
    .in0({32{1'b0}}), .in1(32'h1), .out(multiplexer_8_out), .sel(LessZero));  // open: en

  // Other names for the same wires on the sheet: Address[4:0] = out_7; ALUOut[6:2] = out_7; Func[5:0] = out_2[5:0];
  //   Imm16[15:0] = out_2[15:0]; Instr[31:0] = out_2; instr_index[25:0] = out_2[25:0]; Shamt[4:0] = out_2[10:6];
  //   Rd[4:0] = out_2[15:11]; Rt[4:0] = out_2[20:16]; Rs[4:0] = out_2[25:21]; MemData[31:0] = out_8; MemWrite = out_6;
  //   OpCode[5:0] = out_2[31:26]; RegAddr[4:0] = out_4; RegWrite = out_3; WD[31:0] = out_5

  // Notes on the sheet:
  //   MIPS_LITE1={addu,subu,ori,lui,lw,sw,beq,nop}
  //   MIPS_LITE2={MIPS_LITE1,addi,and,sll,sltiu,slt,bltz,j,jal,jr}
  //   Fetch Instruction
  //   Decode
  //   Excecute
  //   Memory
  //   Output
  //   Write  Back
endmodule

module IFU (
  input  if_beq,
  input  zero,
  input  if_bltz,
  input  LessZero,
  input  if_j,
  input  [31:0] jr_PC,
  input  if_jr,
  input  [31:0] Offset,
  input  Clk,
  input  Reset,
  input  [25:0] instr_index,
  output [31:0] PC4,
  output [31:0] Ins
);

  wire and_1_out, and_2_out, or_1_out;
  wire [27:0] PC;
  wire [31:0] multiplexer_1_out, multiplexer_2_out, NPC, PC_Offset, shifter_1_out;
  wire [31:28] j_dst;

  and and_1 (and_1_out, if_beq, zero);
  and and_2 (and_2_out, if_bltz, LessZero);
  or or_1 (or_1_out, and_1_out, and_2_out);
  Multiplexer #(.width(32)) multiplexer_1 (
    .in0(PC4), .in1(PC_Offset), .out(multiplexer_1_out), .sel(or_1_out));  // open: en
  Multiplexer #(.width(32)) multiplexer_2 (
    .in0(multiplexer_1_out), .in1({j_dst, instr_index, 2'b00}), .out(multiplexer_2_out), .sel(if_j));  // open: en
  Register #(.width(32)) u_PC (.D(NPC), .Q({j_dst, PC}), .clk(Clk), .clr(Reset));  // open: en
  Multiplexer #(.width(32)) multiplexer_3 (.in0(multiplexer_2_out), .in1(jr_PC), .out(NPC), .sel(if_jr));  // open: en
  Adder #(.width(32)) adder_1 (.a(32'h4), .b({j_dst, PC}), .out(PC4));  // open: cin, cout
  Shifter #(.width(32)) shifter_1 (.in(Offset), .\dist (5'b00010), .out(shifter_1_out));
  Adder #(.width(32)) adder_2 (.a(PC4), .b(shifter_1_out), .out(PC_Offset));  // open: cin, cout
  ROM #(.addrWidth(5), .dataWidth(32)) rom_1 (.addr(PC[6:2]), .data(Ins));  // open: sel

  // Other names for the same wires on the sheet: j_dst[27:2] = instr_index; PC[31:28] = j_dst

  // Notes on the sheet:
  //   contents of rom_1 (hex, n*v repeats v):
  //   340004d2 34010001 3402000a 22182a 10600004 12080 ac812000 20210001 8000003 3405000b 2ca60014
  //   10c00004 53880 ace52000 20a50001 800000a
endmodule

module GPR (
  input  [31:0] WD,
  input  [4:0] RW,
  input  Clk,
  input  Reset,
  input  [4:0] RA,
  input  [4:0] RB,
  input  WE,
  output [31:0] BusA,
  output [31:0] BusB
);

  wire En0, en0_t, En1, en1_t, En2, en2_t, En3, en3_t, En4, en4_t, En5, en5_t, En6, en6_t, En7, en7_t, En8,
       en8_t, En9, en9_t, En10, en10_t, En11, en11_t, En12, en12_t, En13, en13_t, En14, en14_t, En15, en15_t,
       En16, en16_t, En17, en17_t, En18, en18_t, En19, en19_t, En20, en20_t, En21, en21_t, En22, en22_t,
       En23, en23_t, En24, en24_t, En25, en25_t, En26, en26_t, En27, en27_t, En28, en28_t, En29, en29_t,
       En30, en30_t, En31, en31_t;
  wire [31:0] _0, _1, _2, _3, _4, _5, _6, _7, _8, _9, _10, _11, _12, _13, _14, _15, _16, _17, _18, _19, _20,
       _21, _22, _23, _24, _25, _26, _27, _28, _29, _30, _31;

  Decoder #(.select(5)) decoder_1 (
    .out0(en0_t), .out1(en1_t), .out2(en2_t), .out3(en3_t), .out4(en4_t), .out5(en5_t), .out6(en6_t),
    .out7(en7_t), .out8(en8_t), .out9(en9_t), .out10(en10_t), .out11(en11_t), .out12(en12_t), .out13(en13_t),
    .out14(en14_t), .out15(en15_t), .out16(en16_t), .out17(en17_t), .out18(en18_t), .out19(en19_t),
    .out20(en20_t), .out21(en21_t), .out22(en22_t), .out23(en23_t), .out24(en24_t), .out25(en25_t),
    .out26(en26_t), .out27(en27_t), .out28(en28_t), .out29(en29_t), .out30(en30_t), .out31(en31_t), .sel(RW));  // open: en
  Multiplexer #(.select(5), .width(32)) multiplexer_1 (
    .in0(_0), .in1(_1), .in2(_2), .in3(_3), .in4(_4), .in5(_5), .in6(_6), .in7(_7), .in8(_8), .in9(_9),
    .in10(_10), .in11(_11), .in12(_12), .in13(_13), .in14(_14), .in15(_15), .in16(_16), .in17(_17),
    .in18(_18), .in19(_19), .in20(_20), .in21(_21), .in22(_22), .in23(_23), .in24(_24), .in25(_25),
    .in26(_26), .in27(_27), .in28(_28), .in29(_29), .in30(_30), .in31(_31), .out(BusA), .sel(RA));  // open: en
  Multiplexer #(.select(5), .width(32)) multiplexer_2 (
    .in0(_0), .in1(_1), .in2(_2), .in3(_3), .in4(_4), .in5(_5), .in6(_6), .in7(_7), .in8(_8), .in9(_9),
    .in10(_10), .in11(_11), .in12(_12), .in13(_13), .in14(_14), .in15(_15), .in16(_16), .in17(_17),
    .in18(_18), .in19(_19), .in20(_20), .in21(_21), .in22(_22), .in23(_23), .in24(_24), .in25(_25),
    .in26(_26), .in27(_27), .in28(_28), .in29(_29), .in30(_30), .in31(_31), .out(BusB), .sel(RB));  // open: en
  and and_1 (En0, en0_t, 1'b0, WE);
  and and_2 (En4, en4_t, WE);
  and and_3 (En8, en8_t, WE);
  and and_4 (En12, en12_t, WE);
  and and_5 (En16, en16_t, WE);
  and and_6 (En20, en20_t, WE);
  and and_7 (En24, en24_t, WE);
  and and_8 (En28, en28_t, WE);
  Register #(.width(32)) register_1 (.D({32{1'b0}}), .en(En0), .Q(_0), .clk(Clk), .clr(Reset));
  Register #(.width(32)) register_2 (.D(WD), .en(En4), .Q(_4), .clk(Clk), .clr(Reset));
  Register #(.width(32)) register_3 (.D(WD), .en(En8), .Q(_8), .clk(Clk), .clr(Reset));
  Register #(.width(32)) register_4 (.D(WD), .en(En12), .Q(_12), .clk(Clk), .clr(Reset));
  Register #(.width(32)) register_5 (.D(WD), .en(En16), .Q(_16), .clk(Clk), .clr(Reset));
  Register #(.width(32)) register_6 (.D(WD), .en(En20), .Q(_20), .clk(Clk), .clr(Reset));
  Register #(.width(32)) register_7 (.D(WD), .en(En24), .Q(_24), .clk(Clk), .clr(Reset));
  Register #(.width(32)) register_8 (.D(WD), .en(En28), .Q(_28), .clk(Clk), .clr(Reset));
  Register #(.width(32)) register_9 (.D(WD), .en(En1), .Q(_1), .clk(Clk), .clr(Reset));
  Register #(.width(32)) register_10 (.D(WD), .en(En5), .Q(_5), .clk(Clk), .clr(Reset));
  Register #(.width(32)) register_11 (.D(WD), .en(En9), .Q(_9), .clk(Clk), .clr(Reset));
  Register #(.width(32)) register_12 (.D(WD), .en(En13), .Q(_13), .clk(Clk), .clr(Reset));
  Register #(.width(32)) register_13 (.D(WD), .en(En17), .Q(_17), .clk(Clk), .clr(Reset));
  Register #(.width(32)) register_14 (.D(WD), .en(En21), .Q(_21), .clk(Clk), .clr(Reset));
  Register #(.width(32)) register_15 (.D(WD), .en(En25), .Q(_25), .clk(Clk), .clr(Reset));
  Register #(.width(32)) register_16 (.D(WD), .en(En29), .Q(_29), .clk(Clk), .clr(Reset));
  and and_9 (En1, en1_t, WE);
  and and_10 (En5, en5_t, WE);
  and and_11 (En9, en9_t, WE);
  and and_12 (En13, en13_t, WE);
  and and_13 (En17, en17_t, WE);
  and and_14 (En21, en21_t, WE);
  and and_15 (En25, en25_t, WE);
  and and_16 (En29, en29_t, WE);
  Register #(.width(32)) register_17 (.D(WD), .en(En2), .Q(_2), .clk(Clk), .clr(Reset));
  Register #(.width(32)) register_18 (.D(WD), .en(En6), .Q(_6), .clk(Clk), .clr(Reset));
  Register #(.width(32)) register_19 (.D(WD), .en(En10), .Q(_10), .clk(Clk), .clr(Reset));
  Register #(.width(32)) register_20 (.D(WD), .en(En14), .Q(_14), .clk(Clk), .clr(Reset));
  Register #(.width(32)) register_21 (.D(WD), .en(En18), .Q(_18), .clk(Clk), .clr(Reset));
  Register #(.width(32)) register_22 (.D(WD), .en(En22), .Q(_22), .clk(Clk), .clr(Reset));
  Register #(.width(32)) register_23 (.D(WD), .en(En26), .Q(_26), .clk(Clk), .clr(Reset));
  Register #(.width(32)) register_24 (.D(WD), .en(En30), .Q(_30), .clk(Clk), .clr(Reset));
  and and_17 (En2, en2_t, WE);
  and and_18 (En6, en6_t, WE);
  and and_19 (En10, en10_t, WE);
  and and_20 (En14, en14_t, WE);
  and and_21 (En18, en18_t, WE);
  and and_22 (En22, en22_t, WE);
  and and_23 (En26, en26_t, WE);
  and and_24 (En30, en30_t, WE);
  Register #(.width(32)) register_25 (.D(WD), .en(En3), .Q(_3), .clk(Clk), .clr(Reset));
  Register #(.width(32)) register_26 (.D(WD), .en(En7), .Q(_7), .clk(Clk), .clr(Reset));
  Register #(.width(32)) register_27 (.D(WD), .en(En11), .Q(_11), .clk(Clk), .clr(Reset));
  Register #(.width(32)) register_28 (.D(WD), .en(En15), .Q(_15), .clk(Clk), .clr(Reset));
  Register #(.width(32)) register_29 (.D(WD), .en(En19), .Q(_19), .clk(Clk), .clr(Reset));
  Register #(.width(32)) register_30 (.D(WD), .en(En23), .Q(_23), .clk(Clk), .clr(Reset));
  Register #(.width(32)) register_31 (.D(WD), .en(En27), .Q(_27), .clk(Clk), .clr(Reset));
  Register #(.width(32)) register_32 (.D(WD), .en(En31), .Q(_31), .clk(Clk), .clr(Reset));
  and and_25 (En3, en3_t, WE);
  and and_26 (En7, en7_t, WE);
  and and_27 (En11, en11_t, WE);
  and and_28 (En15, en15_t, WE);
  and and_29 (En19, en19_t, WE);
  and and_30 (En23, en23_t, WE);
  and and_31 (En27, en27_t, WE);
  and and_32 (En31, en31_t, WE);
endmodule

module ALU (
  input  [31:0] BusA,
  input  [31:0] BusB,
  input  [1:0] ALUOp,
  output [31:0] alu_output,
  output zero,
  output LessZero
);

  wire [31:0] adder_1_out, and_1_out, or_1_out, subtractor_1_out;

  Adder #(.width(32)) adder_1 (.a(BusA), .b(BusB), .out(adder_1_out));  // open: cin, cout
  Subtractor #(.width(32)) subtractor_1 (.a(BusA), .b(BusB), .out(subtractor_1_out));  // open: bin, bout
  assign or_1_out = BusA | BusB;  // OR_Gate or_1, 32 bits wide
  assign and_1_out = BusA & BusB;  // AND_Gate and_1, 32 bits wide
  Comparator #(.width(32)) comparator_1 (.a(BusA), .b(BusB), .eq(zero), .lt(LessZero));  // open: gt
  Multiplexer #(.select(2), .width(32)) multiplexer_1 (
    .in0(adder_1_out), .in1(subtractor_1_out), .in2(or_1_out), .in3(and_1_out), .out(alu_output), .sel(ALUOp));  // open: en
endmodule

module EXT (
  input  [15:0] Imm16,
  input  ExtOp,
  input  LuiOp,
  output [31:0] Ext32
);

  wire [31:0] bit_extender_1_out, bit_extender_2_out, multiplexer_1_out;

  assign bit_extender_1_out = {{16{1'b0}}, Imm16};  // Bit_Extender bit_extender_1
  assign bit_extender_2_out = {{16{Imm16[15]}}, Imm16};  // Bit_Extender bit_extender_2
  Multiplexer #(.width(32)) multiplexer_1 (
    .in0(bit_extender_1_out), .in1(bit_extender_2_out), .out(multiplexer_1_out), .sel(ExtOp));  // open: en
  Multiplexer #(.width(32)) multiplexer_2 (
    .in0(multiplexer_1_out), .in1({Imm16, {16{1'b0}}}), .out(Ext32), .sel(LuiOp));  // open: en
endmodule

module DM (
  input  [4:0] Address,
  input  [31:0] WD,
  input  WE,
  input  Clk,
  input  Reset,
  output [31:0] RD
);

  wire not_1_out;

  not not_1 (not_1_out, WE);
  RAM #(.addrWidth(5), .dataWidth(32), .bus("separate")) ram_1 (
    .addr(Address), .din(WD), .data(RD), .str(WE), .clk(Clk), .ld(not_1_out), .clr(Reset));  // open: sel
endmodule

module CONTROLLER (
  input  [5:0] OpCode,
  input  [5:0] Func,
  output ALUSrc,
  output MemWrite,
  output RegWrite,
  output if_beq,
  output ExtOp,
  output LuiOp,
  output RegDst,
  output MemToReg,
  output [1:0] ALUOp,
  output SllWr,
  output if_bltz,
  output if_j,
  output if_jal,
  output if_jr,
  output if_slt
);

  wire and_1_addi, and_1_addu, and_1_and, and_1_beq, and_1_bltz, and_1_j, and_1_jal, and_1_jr, and_1_lui,
       and_1_lw, and_1_ori, and_1_sll, and_1_slt, and_1_sltiu, and_1_subu, and_1_sw;

  AND and_1 (
    .OpCode(OpCode), .Func(Func), .addu(and_1_addu), .subu(and_1_subu), .ori(and_1_ori), .lui(and_1_lui),
    .lw(and_1_lw), .sw(and_1_sw), .beq(and_1_beq), .addi(and_1_addi), .\and (and_1_and), .sll(and_1_sll),
    .bltz(and_1_bltz), .j(and_1_j), .jal(and_1_jal), .jr(and_1_jr), .slt(and_1_slt), .sltiu(and_1_sltiu));
  OR or_1 (
    .addu(and_1_addu), .subu(and_1_subu), .ori(and_1_ori), .lui(and_1_lui), .lw(and_1_lw), .sw(and_1_sw),
    .beq(and_1_beq), .ALUSrc(ALUSrc), .ALUOp(ALUOp), .MemWrite(MemWrite), .RegWrite(RegWrite),
    .if_beq(if_beq), .ExtOp(ExtOp), .LuiOp(LuiOp), .RegDst(RegDst), .MemToReg(MemToReg), .addi(and_1_addi),
    .\and (and_1_and), .sll(and_1_sll), .SllWr(SllWr), .bltz(and_1_bltz), .if_bltz(if_bltz), .j(and_1_j),
    .if_j(if_j), .if_jal(if_jal), .jal(and_1_jal), .jr(and_1_jr), .if_jr(if_jr), .slt(and_1_slt),
    .sltiu(and_1_sltiu), .if_slt(if_slt));
endmodule

// AND_GATE
module AND (
  input  [5:0] OpCode,
  input  [5:0] Func,
  output addu,
  output subu,
  output ori,
  output lui,
  output lw,
  output sw,
  output beq,
  output addi,
  output \and ,
  output sll,
  output bltz,
  output j,
  output jal,
  output jr,
  output slt,
  output sltiu
);

  wire nF0, nF1, nF2, nF3, nF4, nF5, nop, nOp0, nOp1, nOp2, nOp3, nOp4, nOp5;

  not not_1 (nOp0, OpCode[0]);
  not not_2 (nOp1, OpCode[1]);
  not not_3 (nOp2, OpCode[2]);
  not not_4 (nOp3, OpCode[3]);
  not not_5 (nOp4, OpCode[4]);
  not not_6 (nOp5, OpCode[5]);
  not not_7 (nF0, Func[0]);
  not not_8 (nF1, Func[1]);
  not not_9 (nF2, Func[2]);
  not not_10 (nF3, Func[3]);
  not not_11 (nF4, Func[4]);
  not not_12 (nF5, Func[5]);
  and u_addu (addu, Func[0], nF1, nF2, nop, nF3, nF4, Func[5]);
  and u_subu (subu, Func[0], Func[1], nF2, nop, nF3, nF4, Func[5]);
  and u_ori (ori, OpCode[0], nOp1, OpCode[2], OpCode[3], nOp4, nOp5);
  and u_lui (lui, OpCode[0], OpCode[1], OpCode[2], OpCode[3], nOp4, nOp5);
  and u_lw (lw, OpCode[0], OpCode[1], nOp2, nOp3, nOp4, OpCode[5]);
  and u_sw (sw, OpCode[0], OpCode[1], nOp2, OpCode[3], nOp4, OpCode[5]);
  and u_beq (beq, nOp0, nOp1, OpCode[2], nOp3, nOp4, nOp5);
  and u_nop (nop, nOp0, nOp1, nOp2, nOp3, nOp4, nOp5);
  and u_addi (addi, nOp0, nOp1, nOp2, OpCode[3], nOp4, nOp5);
  and u_and (\and , nF0, nF1, Func[2], nop, nF3, nF4, Func[5]);
  and u_sll (sll, nF0, nF1, nF2, nop, nF3, nF4, nF5);
  and u_bltz (bltz, OpCode[0], nOp1, nOp2, nOp3, nOp4, nOp5);
  and u_j (j, nOp0, OpCode[1], nOp2, nOp3, nOp4, nOp5);
  and u_jal (jal, OpCode[0], OpCode[1], nOp2, nOp3, nOp4, nOp5);
  and u_jr (jr, nF0, nF1, nF2, nop, Func[3], nF4, nF5);
  and u_slt (slt, nF0, Func[1], nF2, nop, Func[3], nF4, Func[5]);
  and u_sltiu (sltiu, OpCode[0], OpCode[1], nOp2, OpCode[3], nOp4, nOp5);

  // Other names for the same wires on the sheet: F0 = Func[0]; F1 = Func[1]; F2 = Func[2]; F3 = Func[3]; F4 = Func[4];
  //   F5 = Func[5]; Op0 = OpCode[0]; Op1 = OpCode[1]; Op2 = OpCode[2]; Op3 = OpCode[3]; Op4 = OpCode[4];
  //   Op5 = OpCode[5]
endmodule

// OR_GATE
module OR (
  input  addu,
  input  subu,
  input  ori,
  input  lui,
  input  lw,
  input  sw,
  input  beq,
  input  addi,
  input  \and ,
  input  sll,
  input  bltz,
  input  j,
  input  jal,
  input  jr,
  input  slt,
  input  sltiu,
  output ALUSrc,
  output [1:0] ALUOp,
  output MemWrite,
  output SllWr,
  output RegWrite,
  output if_bltz,
  output if_beq,
  output if_j,
  output ExtOp,
  output if_jal,
  output if_jr,
  output LuiOp,
  output if_slt,
  output RegDst,
  output MemToReg
);

  or or_1 (ALUSrc, ori, lui, addi, lw, sw, sltiu);
  buf or_2 (MemWrite, sw);  // OR_Gate
  or or_3 (RegWrite, sltiu, sll, \and , addu, subu, ori, lui, lw, addi, slt, jal);
  or or_4 (ExtOp, beq, lw, sw, addi, bltz, sltiu);
  or or_5 (RegDst, addu, subu, \and , sll, slt);
  buf or_6 (MemToReg, lw);  // OR_Gate
  or or_7 (ALUOp[1], ori, \and );
  or or_8 (ALUOp[0], subu, \and );
  or or_9 (if_j, j, jal);
  or or_10 (if_slt, slt, sltiu);

  assign if_beq = beq;
  assign if_bltz = bltz;
  assign if_jal = jal;
  assign if_jr = jr;
  assign LuiOp = lui;
  assign SllWr = sll;
endmodule
