// Logisim project PRE_CPU_0.circ as structural Verilog: 7 circuits, main circuit main
module main (
  input  Reset,
  output [31:0] out_2,
  output out_3,
  output [4:0] out_4,
  output [31:0] out_5,
  output out_6,
  output [4:0] out_7,
  output [31:0] out_8
);

  wire alu_1_zero, ALUSrc, Clk_out, ExtOp, LuiOp, MemToReg, nPC_Sel, RegDst;
  wire [1:0] ALUOp;
  wire [31:0] alu_1_alu_output, dm_1_rd, ext_1_ext32, grf_1_busa, multiplexer_2_out;

  Clock Clk (.out(Clk_out));
  IFU ifu_1 (.Reset(Reset), .Offset(ext_1_ext32), .nPC_sel(nPC_Sel), .zero(alu_1_zero), .Ins(out_2), .Clk(Clk_out));
  Multiplexer #(.width(5)) multiplexer_1 (
    .in0(out_2[20:16]), .in1(out_2[15:11]), .out(out_4), .sel(RegDst));  // open: en
  GRF grf_1 (
    .WD(out_5), .BusA(grf_1_busa), .BusB(out_8), .RW(out_4), .WE(out_3), .RA(out_2[25:21]),
    .RB(out_2[20:16]), .Clk(Clk_out), .Clr(Reset));
  EXT ext_1 (.Imm16(out_2[15:0]), .Ext32(ext_1_ext32), .ExtOp(ExtOp), .LuiOp(LuiOp));
  Multiplexer #(.width(32)) multiplexer_2 (
    .in0(out_8), .in1(ext_1_ext32), .out(multiplexer_2_out), .sel(ALUSrc));  // open: en
  Controller controller_1 (
    .OpCode(out_2[31:26]), .Func(out_2[5:0]), .RegDst(RegDst), .ALUSrc(ALUSrc), .MemToReg(MemToReg),
    .RegWrite(out_3), .MemWrite(out_6), .nPC_Sel(nPC_Sel), .ExtOp(ExtOp), .LuiOp(LuiOp), .ALUOp(ALUOp));
  ALU alu_1 (
    .BusA(grf_1_busa), .BusB(multiplexer_2_out), .ALUop(ALUOp),
    .alu_output({alu_1_alu_output[31:7], out_7, alu_1_alu_output[1:0]}), .zero(alu_1_zero));
  DM dm_1 (.Address(out_7), .WD(out_8), .WE(out_6), .Reset(Reset), .RD(dm_1_rd), .Clk(Clk_out));
  Multiplexer #(.width(32)) multiplexer_3 (
    .in0({alu_1_alu_output[31:7], out_7, alu_1_alu_output[1:0]}), .in1(dm_1_rd), .out(out_5), .sel(MemToReg));  // open: en

  // Other names for the same wires on the sheet: add[4:0] = out_7; imm16[15:0] = out_2[15:0]; Instr[31:0] = out_2;
  //   Rd[4:0] = out_2[15:11]; Rt[4:0] = out_2[20:16]; Rs[4:0] = out_2[25:21]; Memdata[31:0] = out_8; MemWr = out_6;
  //   RegAddr[4:0] = out_4; RegWr = out_3; WD[31:0] = out_5

  // Notes on the sheet:
  //   imm16
  //   imm16
endmodule

module GRF (
  input  WE,
  input  Clk,
  input  Clr,
  input  [31:0] WD,
  input  [4:0] RA,
  input  [4:0] RB,
  input  [4:0] RW,
  output [31:0] BusA,
  output [31:0] BusB
);

  wire and_1_out, and_2_out, and_3_out, and_4_out, and_5_out, and_6_out, and_7_out, and_8_out, and_9_out,
       and_10_out, and_11_out, and_12_out, and_13_out, and_14_out, and_15_out, and_16_out, and_17_out,
       and_18_out, and_19_out, and_20_out, and_21_out, and_22_out, and_23_out, and_24_out, and_25_out,
       and_26_out, and_27_out, and_28_out, and_29_out, and_30_out, and_31_out, and_32_out, decoder_1_out0,
       decoder_1_out1, decoder_1_out2, decoder_1_out3, decoder_1_out4, decoder_1_out5, decoder_1_out6,
       decoder_1_out7, decoder_1_out8, decoder_1_out9, decoder_1_out10, decoder_1_out11, decoder_1_out12,
       decoder_1_out13, decoder_1_out14, decoder_1_out15, decoder_1_out16, decoder_1_out17, decoder_1_out18,
       decoder_1_out19, decoder_1_out20, decoder_1_out21, decoder_1_out22, decoder_1_out23, decoder_1_out24,
       decoder_1_out25, decoder_1_out26, decoder_1_out27, decoder_1_out28, decoder_1_out29, decoder_1_out30,
       decoder_1_out31;
  wire [31:0] register_2_q, register_3_q, register_4_q, register_5_q, register_6_q, register_7_q,
       register_8_q, register_9_q, register_10_q, register_11_q, register_12_q, register_13_q, register_14_q,
       register_15_q, register_16_q, register_17_q, register_18_q, register_19_q, register_20_q,
       register_21_q, register_22_q, register_23_q, register_24_q, register_25_q, register_26_q,
       register_27_q, register_28_q, register_29_q, register_30_q, register_31_q, register_32_q;

  Decoder #(.select(5)) decoder_1 (
    .out0(decoder_1_out0), .out1(decoder_1_out1), .out2(decoder_1_out2), .out3(decoder_1_out3),
    .out4(decoder_1_out4), .out5(decoder_1_out5), .out6(decoder_1_out6), .out7(decoder_1_out7),
    .out8(decoder_1_out8), .out9(decoder_1_out9), .out10(decoder_1_out10), .out11(decoder_1_out11),
    .out12(decoder_1_out12), .out13(decoder_1_out13), .out14(decoder_1_out14), .out15(decoder_1_out15),
    .out16(decoder_1_out16), .out17(decoder_1_out17), .out18(decoder_1_out18), .out19(decoder_1_out19),
    .out20(decoder_1_out20), .out21(decoder_1_out21), .out22(decoder_1_out22), .out23(decoder_1_out23),
    .out24(decoder_1_out24), .out25(decoder_1_out25), .out26(decoder_1_out26), .out27(decoder_1_out27),
    .out28(decoder_1_out28), .out29(decoder_1_out29), .out30(decoder_1_out30), .out31(decoder_1_out31),
    .sel(RW));  // open: en
  and and_1 (and_1_out, WE, decoder_1_out0);
  and and_2 (and_2_out, WE, decoder_1_out1);
  and and_3 (and_3_out, WE, decoder_1_out2);
  and and_4 (and_4_out, WE, decoder_1_out3);
  and and_5 (and_5_out, WE, decoder_1_out4);
  and and_6 (and_6_out, WE, decoder_1_out5);
  and and_7 (and_7_out, WE, decoder_1_out6);
  and and_8 (and_8_out, WE, decoder_1_out7);
  and and_9 (and_9_out, WE, decoder_1_out8);
  and and_10 (and_10_out, WE, decoder_1_out9);
  and and_11 (and_11_out, WE, decoder_1_out10);
  and and_12 (and_12_out, WE, decoder_1_out11);
  and and_13 (and_13_out, WE, decoder_1_out12);
  and and_14 (and_14_out, WE, decoder_1_out13);
  and and_15 (and_15_out, WE, decoder_1_out14);
  and and_16 (and_16_out, WE, decoder_1_out15);
  and and_17 (and_17_out, WE, decoder_1_out16);
  and and_18 (and_18_out, WE, decoder_1_out17);
  and and_19 (and_19_out, WE, decoder_1_out18);
  and and_20 (and_20_out, WE, decoder_1_out19);
  and and_21 (and_21_out, WE, decoder_1_out20);
  and and_22 (and_22_out, WE, decoder_1_out21);
  and and_23 (and_23_out, WE, decoder_1_out22);
  and and_24 (and_24_out, WE, decoder_1_out23);
  and and_25 (and_25_out, WE, decoder_1_out24);
  and and_26 (and_26_out, WE, decoder_1_out25);
  and and_27 (and_27_out, WE, decoder_1_out26);
  and and_28 (and_28_out, WE, decoder_1_out27);
  and and_29 (and_29_out, WE, decoder_1_out28);
  and and_30 (and_30_out, WE, decoder_1_out29);
  and and_31 (and_31_out, WE, decoder_1_out30);
  and and_32 (and_32_out, WE, decoder_1_out31);
  Register #(.width(32)) register_1 (.en(and_1_out), .clk(Clk), .clr(Clr));  // open: D, Q
  Register #(.width(32)) register_2 (.D(WD), .en(and_2_out), .Q(register_2_q), .clk(Clk), .clr(Clr));
  Register #(.width(32)) register_3 (.D(WD), .en(and_3_out), .Q(register_3_q), .clk(Clk), .clr(Clr));
  Register #(.width(32)) register_4 (.D(WD), .en(and_4_out), .Q(register_4_q), .clk(Clk), .clr(Clr));
  Register #(.width(32)) register_5 (.D(WD), .en(and_5_out), .Q(register_5_q), .clk(Clk), .clr(Clr));
  Register #(.width(32)) register_6 (.D(WD), .en(and_6_out), .Q(register_6_q), .clk(Clk), .clr(Clr));
  Register #(.width(32)) register_7 (.D(WD), .en(and_7_out), .Q(register_7_q), .clk(Clk), .clr(Clr));
  Register #(.width(32)) register_8 (.D(WD), .en(and_8_out), .Q(register_8_q), .clk(Clk), .clr(Clr));
  Register #(.width(32)) register_9 (.D(WD), .en(and_9_out), .Q(register_9_q), .clk(Clk), .clr(Clr));
  Register #(.width(32)) register_10 (.D(WD), .en(and_10_out), .Q(register_10_q), .clk(Clk), .clr(Clr));
  Register #(.width(32)) register_11 (.D(WD), .en(and_11_out), .Q(register_11_q), .clk(Clk), .clr(Clr));
  Register #(.width(32)) register_12 (.D(WD), .en(and_12_out), .Q(register_12_q), .clk(Clk), .clr(Clr));
  Register #(.width(32)) register_13 (.D(WD), .en(and_13_out), .Q(register_13_q), .clk(Clk), .clr(Clr));
  Register #(.width(32)) register_14 (.D(WD), .en(and_14_out), .Q(register_14_q), .clk(Clk), .clr(Clr));
  Register #(.width(32)) register_15 (.D(WD), .en(and_15_out), .Q(register_15_q), .clk(Clk), .clr(Clr));
  Register #(.width(32)) register_16 (.D(WD), .en(and_16_out), .Q(register_16_q), .clk(Clk), .clr(Clr));
  Register #(.width(32)) register_17 (.D(WD), .en(and_17_out), .Q(register_17_q), .clk(Clk), .clr(Clr));
  Register #(.width(32)) register_18 (.D(WD), .en(and_18_out), .Q(register_18_q), .clk(Clk), .clr(Clr));
  Register #(.width(32)) register_19 (.D(WD), .en(and_19_out), .Q(register_19_q), .clk(Clk), .clr(Clr));
  Register #(.width(32)) register_20 (.D(WD), .en(and_20_out), .Q(register_20_q), .clk(Clk), .clr(Clr));
  Register #(.width(32)) register_21 (.D(WD), .en(and_21_out), .Q(register_21_q), .clk(Clk), .clr(Clr));
  Register #(.width(32)) register_22 (.D(WD), .en(and_22_out), .Q(register_22_q), .clk(Clk), .clr(Clr));
  Register #(.width(32)) register_23 (.D(WD), .en(and_23_out), .Q(register_23_q), .clk(Clk), .clr(Clr));
  Register #(.width(32)) register_24 (.D(WD), .en(and_24_out), .Q(register_24_q), .clk(Clk), .clr(Clr));
  Register #(.width(32)) register_25 (.D(WD), .en(and_25_out), .Q(register_25_q), .clk(Clk), .clr(Clr));
  Register #(.width(32)) register_26 (.D(WD), .en(and_26_out), .Q(register_26_q), .clk(Clk), .clr(Clr));
  Register #(.width(32)) register_27 (.D(WD), .en(and_27_out), .Q(register_27_q), .clk(Clk), .clr(Clr));
  Register #(.width(32)) register_28 (.D(WD), .en(and_28_out), .Q(register_28_q), .clk(Clk), .clr(Clr));
  Register #(.width(32)) register_29 (.D(WD), .en(and_29_out), .Q(register_29_q), .clk(Clk), .clr(Clr));
  Register #(.width(32)) register_30 (.D(WD), .en(and_30_out), .Q(register_30_q), .clk(Clk), .clr(Clr));
  Register #(.width(32)) register_31 (.D(WD), .en(and_31_out), .Q(register_31_q), .clk(Clk), .clr(Clr));
  Register #(.width(32)) register_32 (.D(WD), .en(and_32_out), .Q(register_32_q), .clk(Clk), .clr(Clr));
  Multiplexer #(.select(5), .width(32)) multiplexer_1 (
    .in0({32{1'b0}}), .in1(register_2_q), .in2(register_3_q), .in3(register_4_q), .in4(register_5_q),
    .in5(register_6_q), .in6(register_7_q), .in7(register_8_q), .in8(register_9_q), .in9(register_10_q),
    .in10(register_11_q), .in11(register_12_q), .in12(register_13_q), .in13(register_14_q),
    .in14(register_15_q), .in15(register_16_q), .in16(register_17_q), .in17(register_18_q),
    .in18(register_19_q), .in19(register_20_q), .in20(register_21_q), .in21(register_22_q),
    .in22(register_23_q), .in23(register_24_q), .in24(register_25_q), .in25(register_26_q),
    .in26(register_27_q), .in27(register_28_q), .in28(register_29_q), .in29(register_30_q),
    .in30(register_31_q), .in31(register_32_q), .out(BusA), .sel(RA));  // open: en
  Multiplexer #(.select(5), .width(32)) multiplexer_2 (
    .in0({32{1'b0}}), .in1(register_2_q), .in2(register_3_q), .in3(register_4_q), .in4(register_5_q),
    .in5(register_6_q), .in6(register_7_q), .in7(register_8_q), .in8(register_9_q), .in9(register_10_q),
    .in10(register_11_q), .in11(register_12_q), .in12(register_13_q), .in13(register_14_q),
    .in14(register_15_q), .in15(register_16_q), .in16(register_17_q), .in17(register_18_q),
    .in18(register_19_q), .in19(register_20_q), .in20(register_21_q), .in21(register_22_q),
    .in22(register_23_q), .in23(register_24_q), .in24(register_25_q), .in25(register_26_q),
    .in26(register_27_q), .in27(register_28_q), .in28(register_29_q), .in29(register_30_q),
    .in30(register_31_q), .in31(register_32_q), .out(BusB), .sel(RB));  // open: en
endmodule

module ALU (
  input  [31:0] BusA,
  input  [31:0] BusB,
  input  [1:0] ALUop,
  output [31:0] alu_output,
  output zero
);

  wire [31:0] adder_1_out, or_1_out, subtractor_1_out;

  Adder #(.width(32)) adder_1 (.a(BusA), .b(BusB), .out(adder_1_out));  // open: cin, cout
  Subtractor #(.width(32)) subtractor_1 (.a(BusA), .b(BusB), .out(subtractor_1_out));  // open: bin, bout
  assign or_1_out = BusA | BusB;  // OR_Gate or_1, 32 bits wide
  Comparator #(.width(32), .mode("unsigned")) comparator_1 (.a(BusA), .b(BusB), .eq(zero));  // open: gt, lt
  Multiplexer #(.select(2), .width(32)) multiplexer_1 (
    .in0(adder_1_out), .in1(subtractor_1_out), .in2(or_1_out), .out(alu_output), .sel(ALUop));  // open: in3, en
endmodule

module EXT (
  input  ExtOp,
  input  LuiOp,
  input  [15:0] Imm16,
  output [31:0] Ext32
);

  wire [31:0] bit_extender_1_out, bit_extender_2_out, multiplexer_1_out;

  assign bit_extender_1_out = {{16{1'b0}}, Imm16};  // Bit_Extender bit_extender_1
  assign bit_extender_2_out = {{16{Imm16[15]}}, Imm16};  // Bit_Extender bit_extender_2
  Multiplexer #(.width(32)) multiplexer_1 (
    .in0(bit_extender_1_out), .in1(bit_extender_2_out), .out(multiplexer_1_out), .sel(ExtOp));  // open: en
  Multiplexer #(.width(32)) multiplexer_2 (
    .in0(multiplexer_1_out), .in1({Imm16, {16{1'b0}}}), .out(Ext32), .sel(LuiOp));  // open: en
endmodule

module DM (
  input  [4:0] Address,
  input  [31:0] WD,
  input  WE,
  input  Reset,
  input  Clk,
  output [31:0] RD
);

  wire not_1_out;

  RAM #(.addrWidth(5), .dataWidth(32), .bus("separate")) ram_1 (
    .addr(Address), .din(WD), .data(RD), .str(WE), .sel(1'b1), .clk(Clk), .ld(not_1_out), .clr(Reset));
  not not_1 (not_1_out, WE);
endmodule

module IFU (
  input  Clk,
  input  Reset,
  input  [31:0] Offset,
  input  nPC_sel,
  input  zero,
  output [31:0] Ins
);

  wire and_1_out;
  wire [31:0] adder_1_out, adder_2_out, multiplexer_1_out, register_1_q;

  Register #(.width(32)) register_1 (.D(multiplexer_1_out), .en(1'b1), .Q(register_1_q), .clk(Clk), .clr(Reset));
  and and_1 (and_1_out, nPC_sel, zero);
  Adder #(.width(32)) adder_1 (.a(register_1_q), .b(32'h4), .out(adder_1_out));  // open: cin, cout
  Adder #(.width(32)) adder_2 (.a(adder_1_out), .b({Offset[29:0], 2'b00}), .out(adder_2_out));  // open: cin, cout
  Multiplexer #(.width(32)) multiplexer_1 (
    .in0(adder_1_out), .in1(adder_2_out), .out(multiplexer_1_out), .sel(and_1_out));  // open: en
  ROM #(.addrWidth(5), .dataWidth(32)) rom_1 (.addr(register_1_q[6:2]), .data(Ins));  // open: sel

  // Notes on the sheet:
  //   contents of rom_1 (hex, n*v repeats v):
  //   341c0000 341d0000 340080f8 36ee0367 3593769c 34dda539 3465c5dc 34be0ff1 3472af1d 35566602 35fe72a7
  //   3437ff23 37b9649e 3690bf9b 37fe4e0c 3711f49d 3c113bfe 3c057433 3c03c451 3c04c431 3c1c24d9 3c1bf0da
  //   3c0ccc68 3c0a118d 3c1021ea 3c0004d3 3c16115b 3c184f06 3c1215de 1000ffff
endmodule

module Controller (
  input  [5:0] OpCode,
  input  [5:0] Func,
  output RegDst,
  output ALUSrc,
  output MemToReg,
  output RegWrite,
  output MemWrite,
  output nPC_Sel,
  output ExtOp,
  output LuiOp,
  output [1:0] ALUOp
);

  wire addu_out, not_1_out, not_2_out, not_3_out, not_4_out, not_5_out, not_6_out, not_7_out, not_8_out,
       not_9_out, not_10_out, not_11_out, not_12_out, null_out, sll_out, subu_out;

  not not_1 (not_1_out, OpCode[5]);
  not not_2 (not_2_out, Func[5]);
  not not_3 (not_3_out, OpCode[3]);
  not not_4 (not_4_out, OpCode[4]);
  not not_5 (not_5_out, Func[3]);
  not not_6 (not_6_out, Func[4]);
  not not_7 (not_7_out, OpCode[1]);
  not not_8 (not_8_out, OpCode[2]);
  not not_9 (not_9_out, Func[1]);
  not not_10 (not_10_out, Func[2]);
  not not_11 (not_11_out, OpCode[0]);
  not not_12 (not_12_out, Func[0]);
  and ori (ALUOp[1], OpCode[0], not_7_out, OpCode[2], OpCode[3], not_4_out, not_1_out);
  and lw (MemToReg, OpCode[0], OpCode[1], not_8_out, not_3_out, not_4_out, OpCode[5]);
  and sw (MemWrite, OpCode[0], OpCode[1], not_8_out, OpCode[3], not_4_out, OpCode[5]);
  and beq (nPC_Sel, not_11_out, not_7_out, OpCode[2], not_3_out, not_4_out, not_1_out);
  and \null  (null_out, not_1_out, not_4_out, not_3_out, not_8_out, not_7_out, not_11_out);
  and lui (LuiOp, OpCode[0], OpCode[1], OpCode[2], OpCode[3], not_4_out, not_1_out);
  and addu (addu_out, Func[0], not_9_out, not_10_out, not_5_out, not_6_out, Func[5], null_out);
  and subu (subu_out, Func[0], Func[1], not_10_out, not_5_out, not_6_out, Func[5], null_out);
  and sll (sll_out, not_12_out, not_9_out, not_10_out, not_5_out, not_6_out, not_2_out, null_out);
  or or_1 (RegDst, addu_out, sll_out, subu_out);
  or or_2 (ALUSrc, ALUOp[1], MemToReg, LuiOp, MemWrite);
  or or_3 (RegWrite, subu_out, addu_out, LuiOp, MemToReg, ALUOp[1], sll_out);
  or or_4 (ExtOp, MemWrite, nPC_Sel, MemToReg);
  or or_5 (ALUOp[0], subu_out, nPC_Sel);

  // Notes on the sheet:
  //   4
  //   5
  //   3
  //   2
  //   1
  //   0
  //   lw
  //   ori
  //   sw
  //   lui
  //   sub
  //   beq
  //   add
  //   sll
endmodule
