// Logisim project assignment2.circ as structural Verilog: 1 circuit, main circuit main
module main (
  input  Guest1,
  input  Guest2,
  input  Guest3,
  input  J
);

  wire clock_1_out, d_ff_1_q, d_ff_2_q, d_ff_3_q, nand_1_out, nand_2_out, nand_3_out, not_1_out, not_2_out,
       not_3_out;

  nand nand_1 (nand_1_out, Guest1, nand_2_out, nand_3_out);
  nand nand_2 (nand_2_out, nand_1_out, Guest2, nand_3_out);
  nand nand_3 (nand_3_out, nand_1_out, nand_2_out, Guest3);
  Clock clock_1 (.out(clock_1_out));
  not not_1 (not_1_out, nand_1_out);
  not not_2 (not_2_out, nand_2_out);
  not not_3 (not_3_out, nand_3_out);
  D_Flip_Flop d_ff_1 (.clk(clock_1_out), .D(not_1_out), .Q(d_ff_1_q), .en(1'b1), .reset(J));  // open: Qn, preset
  D_Flip_Flop d_ff_2 (.clk(clock_1_out), .D(not_2_out), .Q(d_ff_2_q), .en(1'b1), .reset(J));  // open: Qn, preset
  D_Flip_Flop d_ff_3 (.clk(clock_1_out), .D(not_3_out), .Q(d_ff_3_q), .en(1'b1), .reset(J));  // open: Qn, preset
  LED u_Guest1 (.in(d_ff_1_q));
  LED u_Guest2 (.in(d_ff_2_q));
  LED u_Guest3 (.in(d_ff_3_q));
endmodule
