// Logisim project 1-8bit_adder.circ as structural Verilog: 3 circuits, main circuit main
module main (
);

  _8bit_adder u_8bit_adder_1 ();  // open: Cin, A, B, Cout, S
endmodule

module _1bit_adder (
  input  A,
  input  B,
  input  Ci,
  output CO,
  output S0
);

  wire and_1_out, and_2_out, and_3_out, and_4_out, and_5_out, and_6_out, and_7_out, not_1_out, not_2_out,
       not_3_out, not_4_out, not_5_out, not_6_out;

  and and_1 (and_1_out, B, Ci);
  and and_2 (and_2_out, A, Ci);
  and and_3 (and_3_out, A, B);
  not not_1 (not_1_out, A);
  not not_2 (not_2_out, B);
  not not_3 (not_3_out, A);
  not not_4 (not_4_out, Ci);
  not not_5 (not_5_out, B);
  not not_6 (not_6_out, Ci);
  or or_1 (CO, and_1_out, and_2_out, and_3_out);
  and and_4 (and_4_out, not_1_out, not_2_out, Ci);
  and and_5 (and_5_out, not_3_out, B, not_4_out);
  and and_6 (and_6_out, A, not_5_out, not_6_out);
  and and_7 (and_7_out, A, B, Ci);
  or or_2 (S0, and_4_out, and_5_out, and_6_out, and_7_out);
endmodule

module _8bit_adder (
  input  Cin,
  input  [7:0] A,
  input  [7:0] B,
  output Cout,
  output [7:0] S
);

  wire n1bit_adder_1_co, n1bit_adder_2_co, n1bit_adder_3_co, n1bit_adder_4_co, n1bit_adder_5_co,
       n1bit_adder_6_co, n1bit_adder_7_co;

  _1bit_adder u_1bit_adder_1 (.A(A[0]), .B(B[0]), .Ci(Cin), .CO(n1bit_adder_1_co), .S0(S[0]));
  _1bit_adder u_1bit_adder_2 (.A(A[1]), .B(B[1]), .Ci(n1bit_adder_1_co), .CO(n1bit_adder_2_co), .S0(S[1]));
  _1bit_adder u_1bit_adder_3 (.A(A[2]), .B(B[2]), .Ci(n1bit_adder_2_co), .CO(n1bit_adder_3_co), .S0(S[2]));
  _1bit_adder u_1bit_adder_4 (.A(A[3]), .B(B[3]), .Ci(n1bit_adder_3_co), .CO(n1bit_adder_4_co), .S0(S[3]));
  _1bit_adder u_1bit_adder_5 (.A(A[4]), .B(B[4]), .Ci(n1bit_adder_4_co), .CO(n1bit_adder_5_co), .S0(S[4]));
  _1bit_adder u_1bit_adder_6 (.A(A[5]), .B(B[5]), .Ci(n1bit_adder_5_co), .CO(n1bit_adder_6_co), .S0(S[5]));
  _1bit_adder u_1bit_adder_7 (.A(A[6]), .B(B[6]), .Ci(n1bit_adder_6_co), .CO(n1bit_adder_7_co), .S0(S[6]));
  _1bit_adder u_1bit_adder_8 (.A(A[7]), .B(B[7]), .Ci(n1bit_adder_7_co), .CO(Cout), .S0(S[7]));
endmodule
