// Logisim project 2-DATE.circ as structural Verilog: 3 circuits, main circuit main
module main (
  output out_1
);

  wire clock_1_out, rom_1_data;
  wire [7:0] counter_1_q;

  Counter counter_1 (.Q(counter_1_q), .carry(out_1), .clk(clock_1_out));  // open: load, D, count, clr
  Clock clock_1 (.out(clock_1_out));
  ROM #(.dataWidth(1)) rom_1 (.addr(counter_1_q), .data(rom_1_data));  // open: sel
  mod7 mod7_1 (.In(rom_1_data));  // open: S0, S1, S2, S3, S4, S5, S6

  // Notes on the sheet:
  //   contents of rom_1 (hex, n*v repeats v):
  //   0 1 0 0 1
endmodule

module mod7 (
  input  In,
  output S0,
  output S1,
  output S2,
  output S3,
  output S4,
  output S5,
  output S6
);

  wire and_1_out, and_2_out, and_3_out, and_4_out, and_5_out, and_6_out, and_7_out, and_8_out, and_9_out,
       and_10_out, and_11_out, and_12_out, and_13_out, and_14_out, and_15_out, and_16_out, and_17_out,
       and_18_out, and_19_out, and_20_out, and_21_out, and_22_out, and_23_out, clock_1_out, not_1_out,
       not_2_out, not_3_out, not_4_out, not_5_out, not_6_out, not_7_out, not_8_out, not_9_out, not_10_out,
       not_11_out, not_12_out, not_13_out, not_14_out, not_15_out, not_16_out, not_17_out, not_18_out,
       not_19_out, not_20_out, not_21_out, not_22_out, not_23_out, not_24_out, not_25_out, not_26_out,
       not_27_out, not_28_out, not_29_out, not_30_out, not_31_out, not_32_out, not_33_out, not_34_out,
       not_35_out, not_36_out, or_1_out, or_2_out, or_3_out, register_1_q, register_2_q, register_3_q;

  not not_1 (not_1_out, register_3_q);
  not not_2 (not_2_out, In);
  not not_3 (not_3_out, register_1_q);
  not not_4 (not_4_out, register_2_q);
  not not_5 (not_5_out, In);
  not not_6 (not_6_out, register_3_q);
  not not_7 (not_7_out, register_1_q);
  not not_8 (not_8_out, register_2_q);
  not not_9 (not_9_out, register_1_q);
  not not_10 (not_10_out, register_3_q);
  not not_11 (not_11_out, In);
  and and_1 (and_1_out, register_2_q, not_1_out);
  and and_2 (and_2_out, register_2_q, not_2_out);
  and and_3 (and_3_out, register_1_q, register_3_q, In);
  and and_4 (and_4_out, not_3_out, not_4_out, register_3_q);
  and and_5 (and_5_out, register_3_q, not_5_out);
  and and_6 (and_6_out, register_1_q, not_6_out, In);
  and and_7 (and_7_out, not_7_out, not_8_out, In);
  and and_8 (and_8_out, not_9_out, not_10_out, In);
  and and_9 (and_9_out, register_1_q, not_11_out);
  or or_1 (or_1_out, and_1_out, and_2_out, and_3_out);
  or or_2 (or_2_out, and_4_out, and_5_out, and_6_out);
  or or_3 (or_3_out, and_7_out, and_8_out, and_9_out);
  Clock clock_1 (.out(clock_1_out));
  Register #(.width(1)) register_1 (.D(or_1_out), .Q(register_1_q), .clk(clock_1_out));  // open: en, clr
  Register #(.width(1)) register_2 (.D(or_2_out), .Q(register_2_q), .clk(clock_1_out));  // open: en, clr
  Register #(.width(1)) register_3 (.D(or_3_out), .Q(register_3_q), .clk(clock_1_out));  // open: en, clr
  not not_12 (not_12_out, register_1_q);
  not not_13 (not_13_out, register_2_q);
  not not_14 (not_14_out, register_3_q);
  not not_15 (not_15_out, In);
  not not_16 (not_16_out, register_1_q);
  not not_17 (not_17_out, register_2_q);
  not not_18 (not_18_out, register_3_q);
  not not_19 (not_19_out, register_2_q);
  not not_20 (not_20_out, register_3_q);
  not not_21 (not_21_out, In);
  not not_22 (not_22_out, register_1_q);
  not not_23 (not_23_out, register_2_q);
  not not_24 (not_24_out, In);
  not not_25 (not_25_out, register_2_q);
  not not_26 (not_26_out, register_3_q);
  not not_27 (not_27_out, register_1_q);
  not not_28 (not_28_out, register_2_q);
  not not_29 (not_29_out, In);
  not not_30 (not_30_out, register_1_q);
  not not_31 (not_31_out, register_3_q);
  not not_32 (not_32_out, In);
  not not_33 (not_33_out, register_1_q);
  not not_34 (not_34_out, register_3_q);
  not not_35 (not_35_out, In);
  not not_36 (not_36_out, In);
  and and_10 (and_10_out, not_12_out, not_13_out, not_14_out, not_15_out);
  and and_11 (and_11_out, register_2_q, register_3_q, In);
  and and_12 (and_12_out, not_16_out, not_17_out, not_18_out, In);
  and and_13 (and_13_out, register_1_q, not_19_out, not_20_out, not_21_out);
  and and_14 (and_14_out, not_22_out, not_23_out, register_3_q, not_24_out);
  and and_15 (and_15_out, register_1_q, not_25_out, not_26_out, In);
  and and_16 (and_16_out, not_27_out, not_28_out, register_3_q, In);
  and and_17 (and_17_out, register_1_q, register_3_q, not_29_out);
  and and_18 (and_18_out, not_30_out, register_2_q, not_31_out, not_32_out);
  and and_19 (and_19_out, register_1_q, register_3_q, In);
  and and_20 (and_20_out, not_33_out, register_2_q, not_34_out, In);
  and and_21 (and_21_out, register_1_q, register_2_q, not_35_out);
  and and_22 (and_22_out, register_2_q, register_3_q, not_36_out);
  and and_23 (and_23_out, register_1_q, register_2_q, In);
  or or_4 (S0, and_10_out, and_11_out);
  or or_5 (S1, and_12_out, and_13_out);
  or or_6 (S2, and_14_out, and_15_out);
  or or_7 (S3, and_16_out, and_17_out);
  or or_8 (S4, and_18_out, and_19_out);
  or or_9 (S5, and_20_out, and_21_out);
  or or_10 (S6, and_22_out, and_23_out);
endmodule

module MLU (
  input  a,
  input  b,
  input  c,
  input  In,
  output S0,
  output S1,
  output S2,
  output S3,
  output S4,
  output S5,
  output S6
);

  wire and_1_out, and_2_out, and_3_out, and_4_out, and_5_out, and_6_out, and_7_out, and_8_out, and_9_out,
       and_10_out, and_11_out, and_12_out, and_13_out, and_14_out, not_1_out, not_2_out, not_3_out,
       not_4_out, not_5_out, not_6_out, not_7_out, not_8_out, not_9_out, not_10_out, not_11_out, not_12_out,
       not_13_out, not_14_out, not_15_out, not_16_out, not_17_out, not_18_out, not_19_out, not_20_out,
       not_21_out, not_22_out, not_23_out, not_24_out, not_25_out;

  not not_1 (not_1_out, a);
  not not_2 (not_2_out, b);
  not not_3 (not_3_out, c);
  not not_4 (not_4_out, In);
  not not_5 (not_5_out, a);
  not not_6 (not_6_out, b);
  not not_7 (not_7_out, c);
  not not_8 (not_8_out, b);
  not not_9 (not_9_out, c);
  not not_10 (not_10_out, In);
  not not_11 (not_11_out, a);
  not not_12 (not_12_out, b);
  not not_13 (not_13_out, In);
  not not_14 (not_14_out, b);
  not not_15 (not_15_out, c);
  not not_16 (not_16_out, a);
  not not_17 (not_17_out, b);
  not not_18 (not_18_out, In);
  not not_19 (not_19_out, a);
  not not_20 (not_20_out, c);
  not not_21 (not_21_out, In);
  not not_22 (not_22_out, a);
  not not_23 (not_23_out, c);
  not not_24 (not_24_out, In);
  and and_1 (and_1_out, b, c, not_25_out);
  not not_25 (not_25_out, In);
  and and_2 (and_2_out, a, b, In);
  and and_3 (and_3_out, not_1_out, not_2_out, not_3_out, not_4_out);
  or or_1 (S0, and_3_out, and_4_out);
  and and_4 (and_4_out, b, c, In);
  and and_5 (and_5_out, not_5_out, not_6_out, not_7_out, In);
  or or_2 (S1, and_5_out, and_6_out);
  and and_6 (and_6_out, a, not_8_out, not_9_out, not_10_out);
  and and_7 (and_7_out, not_11_out, not_12_out, c, not_13_out);
  or or_3 (S2, and_7_out, and_8_out);
  and and_8 (and_8_out, a, not_14_out, not_15_out, In);
  and and_9 (and_9_out, not_16_out, not_17_out, c, In);
  or or_4 (S3, and_9_out, and_10_out);
  and and_10 (and_10_out, a, c, not_18_out);
  and and_11 (and_11_out, not_19_out, b, not_20_out, not_21_out);
  or or_5 (S4, and_11_out, and_12_out);
  and and_12 (and_12_out, a, c, In);
  and and_13 (and_13_out, not_22_out, b, not_23_out, In);
  or or_6 (S5, and_13_out, and_14_out);
  and and_14 (and_14_out, a, b, not_24_out);
  or or_7 (S6, and_1_out, and_2_out);
endmodule
