// Logisim project 4-fibonacci1.circ as structural Verilog: 2 circuits, main circuit main
module main (
  input  [2:0] N,
  output [3:0] Nth
);

  wire clock_1_out, comparator_1_eq, multiplexer_1_out, not_1_out, register_2_q;
  wire [2:0] adder_1_out, register_1_q;
  wire [3:0] fab_1_out;

  Clock clock_1 (.out(clock_1_out));
  Adder #(.width(3)) adder_1 (.a(3'b001), .b(register_1_q), .out(adder_1_out));  // open: cin, cout
  Register #(.width(3)) register_1 (.D(adder_1_out), .en(1'b1), .Q(register_1_q), .clk(clock_1_out));  // open: clr
  Comparator #(.width(3), .mode("unsigned")) comparator_1 (
    .a(N), .b(register_1_q), .eq(comparator_1_eq));  // open: gt, lt
  FAB fab_1 (.OUT(fab_1_out));
  Register #(.width(1)) register_2 (.D(1'b1), .en(comparator_1_eq), .Q(register_2_q), .clk(clock_1_out));  // open: clr
  not not_1 (not_1_out, 1'b1);
  Multiplexer multiplexer_1 (
    .in0(comparator_1_eq), .in1(not_1_out), .out(multiplexer_1_out), .sel(register_2_q));  // open: en
  Register #(.width(4)) register_3 (.D(fab_1_out), .en(multiplexer_1_out), .Q(Nth), .clk(clock_1_out));  // open: clr
endmodule

module FAB (
  output [3:0] OUT
);

  wire clock_1_out, register_1_q;
  wire [3:0] adder_1_out, multiplexer_1_out, register_3_q;

  Clock clock_1 (.out(clock_1_out));
  Multiplexer #(.width(4)) multiplexer_1 (
    .in0(4'b0001), .in1(OUT), .out(multiplexer_1_out), .sel(register_1_q), .en(1'b1));
  Register #(.width(1)) register_1 (.D(1'b1), .en(1'b1), .Q(register_1_q), .clk(clock_1_out));  // open: clr
  Adder #(.width(4)) adder_1 (.a(register_3_q), .b(multiplexer_1_out), .out(adder_1_out));  // open: cin, cout
  Register #(.width(4)) register_2 (.D(adder_1_out), .en(1'b1), .Q(OUT), .clk(clock_1_out));  // open: clr
  Register #(.width(4)) register_3 (.D(OUT), .en(1'b1), .Q(register_3_q), .clk(clock_1_out));  // open: clr
endmodule
