// Logisim project 5-4bitSort.circ as structural Verilog
module _1bit_swap (
  input  a,
  input  b,
  input  s,
  output A_2,
  output B_2
);

  wire and_1_out, and_2_out, and_3_out, and_4_out, not_1_out, not_2_out;

  not not_1 (not_1_out, s);
  not not_2 (not_2_out, s);
  and and_1 (and_1_out, b, s);
  and and_2 (and_2_out, a, not_1_out);
  and and_3 (and_3_out, b, not_2_out);
  and and_4 (and_4_out, a, s);
  or or_1 (A_2, and_1_out, and_2_out);
  or or_2 (B_2, and_3_out, and_4_out);
endmodule

module _4bit_swap (
  input  [3:0] A,
  input  [3:0] B,
  input  s,
  output [3:0] a_2,
  output [3:0] b_2
);

  _1bit_swap u_1bit_swap_1 (.a(A[0]), .b(B[0]), .s(s), .A_2(a_2[0]), .B_2(b_2[0]));
  _1bit_swap u_1bit_swap_2 (.a(A[2]), .b(B[2]), .s(s), .A_2(a_2[2]), .B_2(b_2[2]));
  _1bit_swap u_1bit_swap_3 (.a(A[1]), .b(B[1]), .s(s), .A_2(a_2[1]), .B_2(b_2[1]));
  _1bit_swap u_1bit_swap_4 (.a(A[3]), .b(B[3]), .s(s), .A_2(a_2[3]), .B_2(b_2[3]));
endmodule

module _4bit_sort (
  input  [3:0] A,
  input  [3:0] B,
  input  [3:0] C,
  input  [3:0] D,
  output [3:0] _1,
  output [3:0] _2,
  output [3:0] _3,
  output [3:0] _4
);

  wire comparator_1_gt, comparator_2_gt, comparator_3_gt, comparator_4_gt, comparator_5_gt;
  wire [3:0] n4bit_swap_1_a_2, n4bit_swap_1_b_2, n4bit_swap_2_a_2, n4bit_swap_2_b_2, n4bit_swap_3_b_2,
       n4bit_swap_4_a_2;

  _4bit_swap u_4bit_swap_1 (.A(A), .B(B), .s(comparator_1_gt), .a_2(n4bit_swap_1_a_2), .b_2(n4bit_swap_1_b_2));
  Comparator #(.width(4), .mode("unsigned")) comparator_1 (.a(A), .b(B), .gt(comparator_1_gt));  // open: eq, lt
  _4bit_swap u_4bit_swap_2 (.A(C), .B(D), .s(comparator_2_gt), .a_2(n4bit_swap_2_a_2), .b_2(n4bit_swap_2_b_2));
  Comparator #(.width(4), .mode("unsigned")) comparator_2 (.a(C), .b(D), .gt(comparator_2_gt));  // open: eq, lt
  Comparator #(.width(4), .mode("unsigned")) comparator_3 (
    .a(n4bit_swap_1_a_2), .b(n4bit_swap_2_a_2), .gt(comparator_3_gt));  // open: eq, lt
  Comparator #(.width(4), .mode("unsigned")) comparator_4 (
    .a(n4bit_swap_1_b_2), .b(n4bit_swap_2_b_2), .gt(comparator_4_gt));  // open: eq, lt
  _4bit_swap u_4bit_swap_3 (
    .A(n4bit_swap_1_a_2), .B(n4bit_swap_2_a_2), .s(comparator_3_gt), .a_2(_1), .b_2(n4bit_swap_3_b_2));
  _4bit_swap u_4bit_swap_4 (
    .A(n4bit_swap_1_b_2), .B(n4bit_swap_2_b_2), .s(comparator_4_gt), .a_2(n4bit_swap_4_a_2), .b_2(_4));
  Comparator #(.width(4), .mode("unsigned")) comparator_5 (
    .a(n4bit_swap_3_b_2), .b(n4bit_swap_4_a_2), .gt(comparator_5_gt));  // open: eq, lt
  _4bit_swap u_4bit_swap_5 (.A(n4bit_swap_3_b_2), .B(n4bit_swap_4_a_2), .s(comparator_5_gt), .a_2(_2), .b_2(_3));
endmodule
