// Logisim project 6-mod5.circ as structural Verilog: 4 circuits, main circuit main
module main (
  output out_1
);

  wire clock_1_out, mod5_1_s0, mod5_1_s1, mod5_1_s2, mod5_1_s3, mod5_1_s4, rom_1_data;
  wire [3:0] counter_1_q;

  Clock clock_1 (.out(clock_1_out));
  Counter #(.width(4), .max('hf)) counter_1 (
    .Q(counter_1_q), .carry(out_1), .clk(clock_1_out));  // open: load, D, count, clr
  ROM #(.addrWidth(4), .dataWidth(1)) rom_1 (.addr(counter_1_q), .data(rom_1_data));  // open: sel
  mod5 mod5_1 (.In(rom_1_data), .s0(mod5_1_s0), .s1(mod5_1_s1), .s2(mod5_1_s2), .s3(mod5_1_s3), .s4(mod5_1_s4));

  // Notes on the sheet:
  //   contents of rom_1 (hex, n*v repeats v):
  //   0 1 0 0 1 0 0 1 0 0 1 0 0 1
endmodule

module fsm (
  input  a,
  input  b,
  input  in,
  output a_,
  output b_
);

  wire and_1_out, and_2_out, not_1_out, not_2_out;

  not not_1 (not_1_out, b);
  not not_2 (not_2_out, in);
  and and_1 (and_1_out, not_1_out, in);
  and and_2 (and_2_out, b, not_2_out);
  or or_1 (b_, and_1_out, and_2_out);

  assign a_ = b;
endmodule

module mod5 (
  input  In,
  output s0,
  output s1,
  output s2,
  output s3,
  output s4
);

  wire and_1_out, and_2_out, clock_1_out, not_1_out, not_2_out, not_3_out, not_4_out, not_5_out, not_6_out,
       or_1_out, register_1_q;

  not not_1 (not_1_out, register_1_q);
  not not_2 (not_2_out, In);
  and and_1 (and_1_out, not_1_out, In);
  and and_2 (and_2_out, register_1_q, not_2_out);
  or or_1 (or_1_out, and_1_out, and_2_out);
  Clock clock_1 (.out(clock_1_out));
  Register #(.width(1)) register_1 (.D(or_1_out), .en(1'b1), .Q(register_1_q), .clk(clock_1_out));  // open: clr
  not not_3 (not_3_out, register_1_q);
  and and_3 (s1, not_3_out, not_4_out);
  not not_4 (not_4_out, In);
  not not_5 (not_5_out, register_1_q);
  and and_4 (s2, not_5_out, In);
  and and_5 (s3, register_1_q, In);
  and and_6 (s4, register_1_q, not_6_out);
  not not_6 (not_6_out, In);

  assign s0 = 1'b0;
endmodule

module \output  (
  input  a,
  input  b,
  input  in,
  output s0,
  output s1,
  output s2,
  output s3,
  output s4
);

  wire not_1_out, not_2_out, not_3_out, not_4_out;

  not not_1 (not_1_out, b);
  not not_2 (not_2_out, in);
  not not_3 (not_3_out, b);
  and and_1 (s3, b, in);
  not not_4 (not_4_out, in);
  and and_2 (s1, not_1_out, not_2_out);
  and and_3 (s2, not_3_out, in);
  and and_4 (s4, b, not_4_out);

  assign s0 = 1'b0;
endmodule
