// Logisim project fb32.circ as structural Verilog: 4 circuits, main circuit main
module main (
  input  [31:0] in_1,
  output [31:0] C11
);

  wire clock_1_out, clock_2_out, clock_3_out, clock_4_out, clock_5_out, clock_6_out, clock_7_out,
       clock_8_out, clock_9_out, k, k1, k2, k3, not_1_out, not_2_out, not_3_out, not_4_out, not_5_out,
       not_6_out, not_7_out;
  wire [31:0] A11, A12, A21, A22, B11, B12, B21, B22, C11_t, C12, C21, C22, counter_1_q, mat_mul_1_c11,
       mat_mul_1_c12, mat_mul_1_c21, mat_mul_1_c22, multiplexer_1_out, multiplexer_2_out, multiplexer_3_out,
       multiplexer_4_out, or_1_out, register_9_q, shifter_1_out, square_1_c11, square_1_c12, square_1_c21,
       square_1_c22;
  wire [31:1] multiplexer_5_out;

  Multiplexer #(.width(32), .enable("false")) multiplexer_1 (.in0(B11), .in1(32'h1), .out(multiplexer_1_out), .sel(k3));
  Multiplexer #(.width(32), .enable("false")) multiplexer_2 (
    .in0(B12), .in1({32{1'b0}}), .out(multiplexer_2_out), .sel(k3));
  Multiplexer #(.width(32), .enable("false")) multiplexer_3 (
    .in0(B21), .in1({32{1'b0}}), .out(multiplexer_3_out), .sel(k3));
  Multiplexer #(.width(32), .enable("false")) multiplexer_4 (.in0(B22), .in1(32'h1), .out(multiplexer_4_out), .sel(k3));
  mat_mul mat_mul_1 (
    .A11(multiplexer_1_out), .A12(multiplexer_2_out), .A21(multiplexer_3_out), .A22(multiplexer_4_out),
    .B11(C11_t), .B12(C12), .B21(C21), .B22(C22), .C11(mat_mul_1_c11), .C12(mat_mul_1_c12),
    .C21(mat_mul_1_c21), .C22(mat_mul_1_c22));
  Multiplexer #(.width(32)) multiplexer_5 (
    .in0(in_1), .in1(register_9_q), .out({multiplexer_5_out, k2}), .sel(not_1_out));  // open: en
  not not_1 (not_1_out, k);
  Multiplexer #(.width(32)) multiplexer_6 (.in0(square_1_c11), .in1(32'h1), .out(C11_t), .sel(k));  // open: en
  Multiplexer #(.width(32)) multiplexer_7 (.in0(square_1_c12), .in1(32'h1), .out(C12), .sel(k));  // open: en
  square square_1 (
    .A11(A11), .A12(A12), .A21(A21), .A22(A22), .C11(square_1_c11), .C12(square_1_c12), .C21(square_1_c21),
    .C22(square_1_c22));
  Multiplexer #(.width(32)) multiplexer_8 (.in0(square_1_c21), .in1(32'h1), .out(C21), .sel(k));  // open: en
  Multiplexer #(.width(32)) multiplexer_9 (.in0(square_1_c22), .in1({32{1'b0}}), .out(C22), .sel(k));  // open: en
  Register #(.width(32)) register_1 (.D(C11_t), .en(not_2_out), .Q(A11), .clk(clock_1_out));  // open: clr
  not not_2 (not_2_out, k1);
  Clock clock_1 (.out(clock_1_out));
  Register #(.width(32)) register_2 (.D(C12), .en(not_3_out), .Q(A12), .clk(clock_2_out));  // open: clr
  not not_3 (not_3_out, k1);
  Clock clock_2 (.out(clock_2_out));
  Register #(.width(32)) register_3 (.D(C21), .en(not_4_out), .Q(A21), .clk(clock_3_out));  // open: clr
  not not_4 (not_4_out, k1);
  Clock clock_3 (.out(clock_3_out));
  Register #(.width(32)) register_4 (.D(C22), .en(not_5_out), .Q(A22), .clk(clock_4_out));  // open: clr
  not not_5 (not_5_out, k1);
  Clock clock_4 (.out(clock_4_out));
  Register #(.width(32)) register_5 (.D(mat_mul_1_c11), .en(k2), .Q(B11), .clk(clock_5_out));  // open: clr
  Clock clock_5 (.out(clock_5_out));
  Register #(.width(32)) register_6 (.D(mat_mul_1_c12), .en(k2), .Q(B12), .clk(clock_6_out));  // open: clr
  Clock clock_6 (.out(clock_6_out));
  Register #(.width(32)) register_7 (.D(mat_mul_1_c21), .en(k2), .Q(B21), .clk(clock_7_out));  // open: clr
  Clock clock_7 (.out(clock_7_out));
  Register #(.width(32)) register_8 (.D(mat_mul_1_c22), .en(k2), .Q(B22), .clk(clock_8_out));  // open: clr
  Clock clock_8 (.out(clock_8_out));
  Shifter #(.width(32), .shift("lr")) shifter_1 (.in({multiplexer_5_out, k2}), .\dist (5'b00001), .out(shifter_1_out));
  Register #(.width(32)) register_9 (
    .D(shifter_1_out), .en(not_6_out), .Q(register_9_q), .clk(clock_9_out));  // open: clr
  not not_6 (not_6_out, k1);
  Clock clock_9 (.out(clock_9_out));
  Counter #(.width(32), .max('hffffffff)) counter_1 (
    .Q(counter_1_q), .clk(clock_9_out));  // open: load, D, count, carry, clr
  Comparator #(.width(32), .mode("unsigned")) comparator_1 (.a(counter_1_q), .b({32{1'b0}}), .eq(k));  // open: gt, lt
  assign or_1_out = B11 | B12 | B21 | B22;  // OR_Gate or_1, 32 bits wide
  Comparator #(.width(32), .mode("unsigned")) comparator_2 (.a(or_1_out), .b({32{1'b0}}), .eq(k3));  // open: gt, lt
  Multiplexer #(.width(32), .enable("false")) multiplexer_10 (.in0(B21), .in1({32{1'b0}}), .out(C11), .sel(not_7_out));
  not not_7 (not_7_out, k1);
  Comparator #(.width(32), .mode("unsigned")) comparator_3 (
    .a({multiplexer_5_out, k2}), .b({32{1'b0}}), .eq(k1));  // open: gt, lt
endmodule

module mul (
  input  [31:0] A11,
  input  [31:0] B11,
  input  [31:0] A12,
  input  [31:0] B21,
  output [31:0] C11
);

  wire [31:0] multiplier_1_out, multiplier_2_out;

  Multiplier #(.width(32)) multiplier_1 (.a(A11), .b(B11), .out(multiplier_1_out));  // open: cin, cout
  Multiplier #(.width(32)) multiplier_2 (.a(A12), .b(B21), .out(multiplier_2_out));  // open: cin, cout
  Adder #(.width(32)) adder_1 (.a(multiplier_1_out), .b(multiplier_2_out), .out(C11));  // open: cin, cout
endmodule

module square (
  input  [31:0] A11,
  input  [31:0] A12,
  input  [31:0] A21,
  input  [31:0] A22,
  output [31:0] C11,
  output [31:0] C12,
  output [31:0] C21,
  output [31:0] C22
);

  mul mul_1 (.A11(A11), .B11(A11), .A12(A12), .B21(A21), .C11(C11));
  mul mul_2 (.A11(A11), .B11(A12), .A12(A12), .B21(A22), .C11(C12));
  mul mul_3 (.A11(A21), .B11(A11), .A12(A22), .B21(A21), .C11(C21));
  mul mul_4 (.A11(A21), .B11(A12), .A12(A22), .B21(A22), .C11(C22));
endmodule

module mat_mul (
  input  [31:0] A11,
  input  [31:0] A12,
  input  [31:0] A21,
  input  [31:0] A22,
  input  [31:0] B11,
  input  [31:0] B12,
  input  [31:0] B21,
  input  [31:0] B22,
  output [31:0] C11,
  output [31:0] C12,
  output [31:0] C21,
  output [31:0] C22
);

  mul mul_1 (.A11(A11), .B11(B11), .A12(A12), .B21(B21), .C11(C11));
  mul mul_2 (.A11(A11), .B11(B12), .A12(A12), .B21(B22), .C11(C12));
  mul mul_3 (.A11(A21), .B11(B11), .A12(A22), .B21(B21), .C11(C21));
  mul mul_4 (.A11(A21), .B11(B12), .A12(A22), .B21(B22), .C11(C22));
endmodule
