// Logisim project 1-spiltter.circ as structural Verilog: 1 circuit, main circuit main
module main (
  input  [5:0] in_1
);

  wire [2:0] xor_1_out;

  // Probe on in_1[3:1]
  // Probe on {in_1[5:4], in_1[0]}
  assign xor_1_out = in_1[3:1] ^ {in_1[5:4], in_1[0]};  // XOR_Gate xor_1, 3 bits wide
  // Probe on xor_1_out
endmodule
