// Logisim project 3-MUX&DECO.circ as structural Verilog: 1 circuit, main circuit main
module main (
  input  A,
  input  B,
  input  C,
  input  D,
  input  in_5
);

  wire decoder_1_out0, decoder_1_out1, decoder_1_out2, decoder_1_out3, multiplexer_1_out;

  LED led_1 (.in(multiplexer_1_out));
  Multiplexer #(.select(2)) multiplexer_1 (
    .in0(A), .in1(B), .in2(C), .in3(D), .out(multiplexer_1_out), .en(in_5));  // open: sel
  Decoder #(.select(2)) decoder_1 (
    .out0(decoder_1_out0), .out1(decoder_1_out1), .out2(decoder_1_out2), .out3(decoder_1_out3), .en(in_5));  // open: sel
  LED led_2 (.in(decoder_1_out0));
  LED led_3 (.in(decoder_1_out1));
  LED led_4 (.in(decoder_1_out2));
  LED led_5 (.in(decoder_1_out3));
endmodule
