// Logisim project 5-4bit_sort.circ as structural Verilog
module _1bit_swap (
  input  I1,
  input  I2,
  input  S,
  output O1,
  output O2
);

  wire and_1_out, and_2_out, and_3_out, and_4_out, not_1_out, not_2_out;

  not not_1 (not_1_out, S);
  not not_2 (not_2_out, S);
  and and_1 (and_1_out, I2, S);
  and and_2 (and_2_out, I1, not_1_out);
  and and_3 (and_3_out, I2, not_2_out);
  and and_4 (and_4_out, I1, S);
  or or_1 (O1, and_1_out, and_2_out);
  or or_2 (O2, and_3_out, and_4_out);
endmodule

module _4bit_swap (
  input  [3:0] i1,
  input  [3:0] i2,
  input  s,
  output [3:0] o1,
  output [3:0] o2
);

  _1bit_swap u_1bit_swap_1 (.I1(i1[0]), .I2(i2[0]), .S(s), .O1(o1[0]), .O2(o2[0]));
  _1bit_swap u_1bit_swap_2 (.I1(i1[1]), .I2(i2[1]), .S(s), .O1(o1[1]), .O2(o2[1]));
  _1bit_swap u_1bit_swap_3 (.I1(i1[2]), .I2(i2[2]), .S(s), .O1(o1[2]), .O2(o2[2]));
  _1bit_swap u_1bit_swap_4 (.I1(i1[3]), .I2(i2[3]), .S(s), .O1(o1[3]), .O2(o2[3]));
endmodule

module _4bit_sort (
  input  [3:0] A,
  input  [3:0] B,
  input  [3:0] C,
  input  [3:0] D,
  output [3:0] _1,
  output [3:0] _2,
  output [3:0] _3,
  output [3:0] _4
);

  wire comparator_1_gt, comparator_2_gt, comparator_3_gt, comparator_4_gt, comparator_5_gt, comparator_6_gt;
  wire [3:0] n4bit_swap_1_o1, n4bit_swap_1_o2, n4bit_swap_2_o1, n4bit_swap_2_o2, n4bit_swap_3_o1,
       n4bit_swap_4_o1, n4bit_swap_4_o2, n4bit_swap_5_o1;

  Comparator #(.width(4), .mode("unsigned")) comparator_1 (.a(A), .b(B), .gt(comparator_1_gt));  // open: eq, lt
  _4bit_swap u_4bit_swap_1 (.i1(A), .i2(B), .s(comparator_1_gt), .o1(n4bit_swap_1_o1), .o2(n4bit_swap_1_o2));
  Comparator #(.width(4), .mode("unsigned")) comparator_2 (
    .a(n4bit_swap_1_o2), .b(C), .gt(comparator_2_gt));  // open: eq, lt
  _4bit_swap u_4bit_swap_2 (
    .i1(n4bit_swap_1_o2), .i2(C), .s(comparator_2_gt), .o1(n4bit_swap_2_o1), .o2(n4bit_swap_2_o2));
  Comparator #(.width(4), .mode("unsigned")) comparator_3 (
    .a(n4bit_swap_2_o2), .b(D), .gt(comparator_3_gt));  // open: eq, lt
  _4bit_swap u_4bit_swap_3 (.i1(n4bit_swap_2_o2), .i2(D), .s(comparator_3_gt), .o1(n4bit_swap_3_o1), .o2(_4));
  Comparator #(.width(4), .mode("unsigned")) comparator_4 (
    .a(n4bit_swap_1_o1), .b(n4bit_swap_2_o1), .gt(comparator_4_gt));  // open: eq, lt
  _4bit_swap u_4bit_swap_4 (
    .i1(n4bit_swap_1_o1), .i2(n4bit_swap_2_o1), .s(comparator_4_gt), .o1(n4bit_swap_4_o1),
    .o2(n4bit_swap_4_o2));
  Comparator #(.width(4), .mode("unsigned")) comparator_5 (
    .a(n4bit_swap_4_o2), .b(n4bit_swap_3_o1), .gt(comparator_5_gt));  // open: eq, lt
  _4bit_swap u_4bit_swap_5 (
    .i1(n4bit_swap_4_o2), .i2(n4bit_swap_3_o1), .s(comparator_5_gt), .o1(n4bit_swap_5_o1), .o2(_3));
  Comparator #(.width(4), .mode("unsigned")) comparator_6 (
    .a(n4bit_swap_4_o1), .b(n4bit_swap_5_o1), .gt(comparator_6_gt));  // open: eq, lt
  _4bit_swap u_4bit_swap_6 (.i1(n4bit_swap_4_o1), .i2(n4bit_swap_5_o1), .s(comparator_6_gt), .o1(_1), .o2(_2));

  // Notes on the sheet:
  //   a
  //   b
  //   b
  //   c
  //   b
  //   c
  //   a
endmodule
