// Logisim project 6-Moore_traffic.circ as structural Verilog
module main (
  input  Ta,
  input  Tb,
  output La1,
  output La0,
  output Lb1,
  output La1_2
);

  wire and_1_out, and_2_out, clock_1_out, not_1_out, not_2_out, not_3_out, not_4_out, not_5_out, not_6_out,
       or_1_out, register_2_q, xor_1_out;

  not not_1 (not_1_out, La1);
  and and_1 (and_1_out, not_1_out, not_2_out, not_3_out);
  not not_2 (not_2_out, register_2_q);
  not not_3 (not_3_out, Ta);
  and and_2 (and_2_out, La1, not_4_out, not_5_out);
  not not_4 (not_4_out, register_2_q);
  not not_5 (not_5_out, Tb);
  xor xor_1 (xor_1_out, La1, register_2_q);
  or or_1 (or_1_out, and_1_out, and_2_out);
  Register #(.width(1)) register_1 (.D(xor_1_out), .Q(La1), .clk(clock_1_out));  // open: en, clr
  Register #(.width(1)) register_2 (.D(or_1_out), .Q(register_2_q), .clk(clock_1_out));  // open: en, clr
  Clock clock_1 (.out(clock_1_out));
  not not_6 (not_6_out, La1);
  and and_3 (La0, not_6_out, register_2_q);
  not not_7 (Lb1, La1);
  and and_4 (La1_2, La1, register_2_q);

  // Notes on the sheet:
  //   S1'
  //   S0'
  //   S1
  //   S0
endmodule
