// Logisim project 7-mod5.circ as structural Verilog: 2 circuits, main circuit mod5
module mod5 (
  input  In,
  output S0,
  output S1,
  output S2,
  output S3,
  output S4
);

  wire clock_1_out, not_1_out, not_2_out, not_3_out, not_4_out, register_2_q;

  Register #(.width(1)) register_1 (.D(register_2_q), .en(1'b1), .clk(clock_1_out));  // open: Q, clr
  Register #(.width(1)) register_2 (.D(In), .en(1'b1), .Q(register_2_q), .clk(clock_1_out));  // open: clr
  Clock clock_1 (.out(clock_1_out));
  not not_1 (not_1_out, register_2_q);
  not not_2 (not_2_out, In);
  not not_3 (not_3_out, register_2_q);
  not not_4 (not_4_out, In);
  and and_1 (S1, not_1_out, not_2_out);
  and and_2 (S2, not_3_out, In);
  and and_3 (S3, register_2_q, In);
  and and_4 (S4, register_2_q, not_4_out);

  assign S0 = 1'b0;

  // Notes on the sheet:
  //   S1
  //   S1'
  //   S0
  //   S0'
endmodule

module main (
  output out_1,
  output out_2,
  output out_3,
  output out_4,
  output out_5
);

  wire clock_1_out, rom_1_data;
  wire [3:0] counter_1_q;

  Clock clock_1 (.out(clock_1_out));
  Counter #(.width(4), .max('hf), .ongoal("stay")) counter_1 (
    .Q(counter_1_q), .clk(clock_1_out));  // open: load, D, count, carry, clr
  ROM #(.addrWidth(4), .dataWidth(1)) rom_1 (.addr(counter_1_q), .data(rom_1_data));  // open: sel
  mod5 mod5_1 (.In(rom_1_data), .S0(out_1), .S1(out_2), .S2(out_3), .S3(out_4), .S4(out_5));

  // Notes on the sheet:
  //   contents of rom_1 (hex, n*v repeats v):
  //   0 1 0 0 1 0 0 1 0 0 1 0 0 1
endmodule
