// Logisim project 7-mod5_modified1.circ as structural Verilog
module mod5 (
  input  In,
  output S0,
  output S1,
  output S2,
  output S3,
  output S4
);

  wire clock_1_out, not_1_out, not_2_out, not_3_out, not_4_out, register_2_q;

  Register #(.width(1)) register_1 (.D(register_2_q), .en(1'b1), .clk(clock_1_out));  // open: Q, clr
  Register #(.width(1)) register_2 (.D(In), .en(1'b1), .Q(register_2_q), .clk(clock_1_out));  // open: clr
  Clock clock_1 (.out(clock_1_out));
  not not_1 (not_1_out, register_2_q);
  not not_2 (not_2_out, In);
  not not_3 (not_3_out, register_2_q);
  not not_4 (not_4_out, In);
  and and_1 (S1, not_1_out, not_2_out);
  and and_2 (S2, not_3_out, In);
  and and_3 (S3, register_2_q, In);
  and and_4 (S4, register_2_q, not_4_out);

  assign S0 = 1'b0;
endmodule
