// Logisim project 7-wrong_version_of_mod5.circ as structural Verilog: 1 circuit, main circuit main
module main (
  input  In,
  output S0,
  output S1,
  output S2,
  output S3,
  output S4
);

  wire and_1_out, and_2_out, and_3_out, and_4_out, and_5_out, and_6_out, clock_1_out, not_1_out, not_2_out,
       not_3_out, not_4_out, not_5_out, not_6_out, not_7_out, not_8_out, not_9_out, not_10_out, not_11_out,
       not_12_out, not_13_out, not_14_out, not_15_out, not_16_out, not_17_out, not_18_out, not_19_out,
       not_20_out, not_21_out, not_22_out, or_1_out, or_2_out, register_1_q, register_2_q, register_3_q;

  not not_1 (not_1_out, register_1_q);
  not not_2 (not_2_out, In);
  not not_3 (not_3_out, register_1_q);
  not not_4 (not_4_out, register_2_q);
  not not_5 (not_5_out, register_3_q);
  not not_6 (not_6_out, register_1_q);
  not not_7 (not_7_out, register_3_q);
  not not_8 (not_8_out, In);
  not not_9 (not_9_out, register_1_q);
  not not_10 (not_10_out, register_2_q);
  not not_11 (not_11_out, register_3_q);
  not not_12 (not_12_out, In);
  and and_1 (and_1_out, not_1_out, register_3_q, not_2_out);
  and and_2 (and_2_out, not_3_out, In);
  and and_3 (and_3_out, register_1_q, not_4_out, not_5_out, In);
  and and_4 (and_4_out, not_6_out, not_7_out, not_8_out);
  and and_5 (and_5_out, not_9_out, register_3_q, In);
  and and_6 (and_6_out, register_1_q, not_10_out, not_11_out, not_12_out);
  or or_1 (or_1_out, and_2_out, and_3_out);
  or or_2 (or_2_out, and_4_out, and_5_out, and_6_out);
  Clock clock_1 (.out(clock_1_out));
  Register #(.width(1)) register_1 (.D(and_1_out), .en(1'b1), .Q(register_1_q), .clk(clock_1_out));  // open: clr
  Register #(.width(1)) register_2 (.D(or_1_out), .en(1'b1), .Q(register_2_q), .clk(clock_1_out));  // open: clr
  Register #(.width(1)) register_3 (.D(or_2_out), .en(1'b1), .Q(register_3_q), .clk(clock_1_out));  // open: clr
  not not_13 (not_13_out, register_1_q);
  not not_14 (not_14_out, register_2_q);
  not not_15 (not_15_out, register_3_q);
  not not_16 (not_16_out, register_1_q);
  not not_17 (not_17_out, register_2_q);
  not not_18 (not_18_out, register_1_q);
  not not_19 (not_19_out, register_3_q);
  not not_20 (not_20_out, register_1_q);
  not not_21 (not_21_out, register_2_q);
  not not_22 (not_22_out, register_2_q);
  and and_7 (S0, not_13_out, not_14_out, not_15_out);
  and and_8 (S1, not_16_out, not_17_out, register_3_q);
  and and_9 (S2, not_18_out, register_2_q, not_19_out);
  and and_10 (S3, not_20_out, register_2_q, register_3_q);
  and and_11 (S4, register_1_q, not_21_out, not_22_out);

  // Notes on the sheet:
  //   S2
  //   S0
  //   I
  //   S1
  //   S2'
  //   S1'
  //   S0'
  //   S2
  //   S1
  //   S0
endmodule
