// Logisim project 8-fibonacci++.circ as structural Verilog: 3 circuits, main circuit main
module main (
  input  [31:0] N,
  output [31:0] Nth
);

  wire clock_1_out, clock_2_out, clock_3_out, comparator_1_eq, multiplexer_2_out, register_2_q, register_3_q,
       register_5_q, register_6_q;
  wire [31:0] mult2_1_out, multiplexer_1_out, register_1_q, register_4_q, shifter_1_out;

  Clock clock_1 (.out(clock_1_out));
  Register #(.width(32)) register_1 (.D(N), .en(1'b1), .Q(register_1_q), .clk(clock_1_out));  // open: clr
  Register #(.width(1)) register_2 (.D(register_3_q), .en(1'b1), .Q(register_2_q), .clk(clock_1_out));  // open: clr
  Register #(.width(1)) register_3 (.D(1'b1), .en(1'b1), .Q(register_3_q), .clk(clock_1_out));  // open: clr
  Multiplexer #(.width(32)) multiplexer_1 (
    .in0(register_1_q), .in1(shifter_1_out), .out(multiplexer_1_out), .sel(register_2_q));  // open: en
  Register #(.width(32)) register_4 (
    .D(multiplexer_1_out), .en(1'b1), .Q(register_4_q), .clk(clock_1_out));  // open: clr
  Shifter #(.width(32), .shift("lr")) shifter_1 (.in(register_4_q), .\dist (5'b00001), .out(shifter_1_out));
  // Probe on shifter_1_out
  Comparator #(.width(32), .mode("unsigned")) comparator_1 (
    .a(multiplexer_1_out), .b({32{1'b0}}), .eq(comparator_1_eq));  // open: gt, lt
  Clock clock_2 (.out(clock_2_out));
  mult2 mult2_1 (.en(multiplexer_1_out[0]), .out(mult2_1_out));
  Register #(.width(1)) register_5 (
    .D(register_6_q), .en(comparator_1_eq), .Q(register_5_q), .clk(clock_2_out));  // open: clr
  Register #(.width(1)) register_6 (.D(1'b1), .en(comparator_1_eq), .Q(register_6_q), .clk(clock_2_out));  // open: clr
  Multiplexer multiplexer_2 (
    .in0(comparator_1_eq), .in1(1'b0), .out(multiplexer_2_out), .sel(register_5_q));  // open: en
  Register #(.width(32)) register_7 (.D(mult2_1_out), .en(multiplexer_2_out), .Q(Nth), .clk(clock_3_out));  // open: clr
  Clock clock_3 (.out(clock_3_out));
endmodule

module mult (
  output [31:0] a,
  output [31:0] b,
  output [31:0] c,
  output [31:0] d
);

  wire clk, register_1_q;
  wire [31:0] in_a, in_b, in_c, in_d, multiplexer_1_out, multiplexer_2_out, multiplexer_3_out,
       multiplexer_4_out, multiplier_1_out, multiplier_2_out, multiplier_3_out, multiplier_4_out,
       multiplier_5_out, multiplier_6_out, multiplier_7_out, multiplier_8_out;

  Clock clock_1 (.out(clk));
  Multiplier #(.width(32)) multiplier_1 (.a(a), .b(a), .out(multiplier_1_out));  // open: cin, cout
  Multiplier #(.width(32)) multiplier_2 (.a(c), .b(b), .out(multiplier_2_out));  // open: cin, cout
  Multiplier #(.width(32)) multiplier_3 (.a(a), .b(b), .out(multiplier_3_out));  // open: cin, cout
  Multiplier #(.width(32)) multiplier_4 (.a(b), .b(d), .out(multiplier_4_out));  // open: cin, cout
  Multiplier #(.width(32)) multiplier_5 (.a(c), .b(a), .out(multiplier_5_out));  // open: cin, cout
  Multiplier #(.width(32)) multiplier_6 (.a(d), .b(c), .out(multiplier_6_out));  // open: cin, cout
  Multiplier #(.width(32)) multiplier_7 (.a(c), .b(b), .out(multiplier_7_out));  // open: cin, cout
  Multiplier #(.width(32)) multiplier_8 (.a(d), .b(d), .out(multiplier_8_out));  // open: cin, cout
  Adder #(.width(32)) adder_1 (.a(multiplier_1_out), .b(multiplier_2_out), .out(in_a));  // open: cin, cout
  Adder #(.width(32)) adder_2 (.a(multiplier_3_out), .b(multiplier_4_out), .out(in_b));  // open: cin, cout
  Adder #(.width(32)) adder_3 (.a(multiplier_5_out), .b(multiplier_6_out), .out(in_c));  // open: cin, cout
  Adder #(.width(32)) adder_4 (.a(multiplier_7_out), .b(multiplier_8_out), .out(in_d));  // open: cin, cout
  Multiplexer #(.width(32)) multiplexer_1 (
    .in0(32'h1), .in1(in_a), .out(multiplexer_1_out), .sel(register_1_q));  // open: en
  Multiplexer #(.width(32)) multiplexer_2 (
    .in0(32'h1), .in1(in_c), .out(multiplexer_2_out), .sel(register_1_q));  // open: en
  Register #(.width(32)) u_a (.D(multiplexer_1_out), .en(1'b1), .Q(a), .clk(clk));  // open: clr
  Register #(.width(32)) u_c (.D(multiplexer_2_out), .en(1'b1), .Q(c), .clk(clk));  // open: clr
  Register #(.width(1)) register_1 (.D(1'b1), .en(1'b1), .Q(register_1_q), .clk(clk));  // open: clr
  Multiplexer #(.width(32)) multiplexer_3 (
    .in0(32'h1), .in1(in_b), .out(multiplexer_3_out), .sel(register_1_q));  // open: en
  Multiplexer #(.width(32)) multiplexer_4 (
    .in0({32{1'b0}}), .in1(in_d), .out(multiplexer_4_out), .sel(register_1_q));  // open: en
  Register #(.width(32)) u_b (.D(multiplexer_3_out), .en(1'b1), .Q(b), .clk(clk));  // open: clr
  Register #(.width(32)) u_d (.D(multiplexer_4_out), .en(1'b1), .Q(d), .clk(clk));  // open: clr

  // Other names for the same wires on the sheet: out_a[31:0] = a; out_b[31:0] = b; out_c[31:0] = c; out_d[31:0] = d
endmodule

module mult2 (
  input  en,
  output [31:0] out
);

  wire clock_1_out, clock_2_out, multiplexer_5_out, register_1_q;
  wire [31:0] a_out, a_q, b_out, c_out, c_q, d_out, d_q, mult_1_a, mult_1_b, mult_1_c, mult_1_d,
       multiplexer_1_out, multiplexer_2_out, multiplexer_3_out, multiplexer_4_out, multiplier_1_out,
       multiplier_2_out, multiplier_3_out, multiplier_4_out, multiplier_5_out, multiplier_6_out,
       multiplier_7_out, multiplier_8_out;

  Register #(.width(1)) register_1 (.D(1'b1), .en(1'b1), .Q(register_1_q), .clk(clock_1_out));  // open: clr
  Clock clock_1 (.out(clock_1_out));
  Multiplexer #(.width(32)) multiplexer_1 (
    .in0(32'h1), .in1(a_out), .out(multiplexer_1_out), .sel(register_1_q));  // open: en
  Multiplexer #(.width(32)) multiplexer_2 (
    .in0({32{1'b0}}), .in1(b_out), .out(multiplexer_2_out), .sel(register_1_q));  // open: en
  Multiplexer #(.width(32)) multiplexer_3 (
    .in0({32{1'b0}}), .in1(c_out), .out(multiplexer_3_out), .sel(register_1_q));  // open: en
  Multiplexer #(.width(32)) multiplexer_4 (
    .in0(32'h1), .in1(d_out), .out(multiplexer_4_out), .sel(register_1_q));  // open: en
  Multiplexer multiplexer_5 (.in0(1'b1), .in1(en), .out(multiplexer_5_out), .sel(register_1_q));  // open: en
  Clock clock_2 (.out(clock_2_out));
  Register #(.width(32)) a (.D(multiplexer_1_out), .en(multiplexer_5_out), .Q(a_q), .clk(clock_2_out));  // open: clr
  Register #(.width(32)) b (.D(multiplexer_2_out), .en(multiplexer_5_out), .Q(out), .clk(clock_2_out));  // open: clr
  Register #(.width(32)) c (.D(multiplexer_3_out), .en(multiplexer_5_out), .Q(c_q), .clk(clock_2_out));  // open: clr
  Register #(.width(32)) d (.D(multiplexer_4_out), .en(multiplexer_5_out), .Q(d_q), .clk(clock_2_out));  // open: clr
  mult mult_1 (.a(mult_1_a), .b(mult_1_b), .c(mult_1_c), .d(mult_1_d));
  Multiplier #(.width(32)) multiplier_1 (.a(a_q), .b(mult_1_a), .out(multiplier_1_out));  // open: cin, cout
  Multiplier #(.width(32)) multiplier_2 (.a(out), .b(mult_1_c), .out(multiplier_2_out));  // open: cin, cout
  Multiplier #(.width(32)) multiplier_3 (.a(a_q), .b(mult_1_b), .out(multiplier_3_out));  // open: cin, cout
  Multiplier #(.width(32)) multiplier_4 (.a(out), .b(mult_1_d), .out(multiplier_4_out));  // open: cin, cout
  Multiplier #(.width(32)) multiplier_5 (.a(c_q), .b(mult_1_a), .out(multiplier_5_out));  // open: cin, cout
  Multiplier #(.width(32)) multiplier_6 (.a(d_q), .b(mult_1_c), .out(multiplier_6_out));  // open: cin, cout
  Multiplier #(.width(32)) multiplier_7 (.a(c_q), .b(mult_1_b), .out(multiplier_7_out));  // open: cin, cout
  Multiplier #(.width(32)) multiplier_8 (.a(d_q), .b(mult_1_d), .out(multiplier_8_out));  // open: cin, cout
  Adder #(.width(32)) adder_1 (.a(multiplier_1_out), .b(multiplier_2_out), .out(a_out));  // open: cin, cout
  Adder #(.width(32)) adder_2 (.a(multiplier_3_out), .b(multiplier_4_out), .out(b_out));  // open: cin, cout
  Adder #(.width(32)) adder_3 (.a(multiplier_5_out), .b(multiplier_6_out), .out(c_out));  // open: cin, cout
  Adder #(.width(32)) adder_4 (.a(multiplier_7_out), .b(multiplier_8_out), .out(d_out));  // open: cin, cout
endmodule
