// Logisim project 8-fibonacci.circ as structural Verilog: 1 circuit, main circuit main
module main (
  input  [2:0] N,
  output [3:0] Nth
);

  wire and_1_out, and_2_out, and_5_out, and_6_out, and_7_out, and_8_out, not_1_out, not_2_out, not_3_out,
       not_4_out, not_5_out, not_6_out, not_7_out, not_8_out, not_9_out;

  not not_1 (not_1_out, N[2]);
  and and_1 (and_1_out, not_1_out, N[1], N[0]);
  not not_2 (not_2_out, N[1]);
  and and_2 (and_2_out, N[2], not_2_out, not_3_out);
  not not_3 (not_3_out, N[0]);
  and and_3 (Nth[2], N[0], N[2]);
  and and_4 (Nth[3], N[1], N[2]);
  not not_4 (not_4_out, N[2]);
  and and_5 (and_5_out, not_4_out, not_5_out, N[0]);
  not not_5 (not_5_out, N[1]);
  not not_6 (not_6_out, N[2]);
  and and_6 (and_6_out, not_6_out, N[1], not_7_out);
  not not_7 (not_7_out, N[0]);
  not not_8 (not_8_out, N[1]);
  and and_7 (and_7_out, N[2], not_8_out, not_9_out);
  not not_9 (not_9_out, N[0]);
  and and_8 (and_8_out, N[2], N[0]);
  or or_1 (Nth[1], and_1_out, and_2_out);
  or or_2 (Nth[0], and_5_out, and_6_out, and_7_out, and_8_out);

  // Notes on the sheet:
  //   A
  //   C
  //   B
  //   C
  //   B
  //   A
endmodule
