// Logisim project 8-fibonacci_modify.circ as structural Verilog: 2 circuits, main circuit main
module main (
  input  [2:0] N,
  output [3:0] Nth
);

  wire clock_1_out, clock_2_out, clock_3_out, comparator_1_eq, multiplexer_1_out, register_3_q;
  wire [2:0] adder_1_out, register_1_q, subtractor_1_out;
  wire [3:0] fab_1_out_1;

  Clock clock_1 (.out(clock_1_out));
  Adder #(.width(3)) adder_1 (.a(3'b001), .b(register_1_q), .out(adder_1_out));  // open: cin, cout
  Register #(.width(3)) register_1 (.D(adder_1_out), .en(1'b1), .Q(register_1_q), .clk(clock_1_out));  // open: clr
  Subtractor #(.width(3)) subtractor_1 (.a(N), .b(3'b001), .out(subtractor_1_out));  // open: bin, bout
  Fab fab_1 (.out_1(fab_1_out_1));
  Comparator #(.width(3)) comparator_1 (.a(register_1_q), .b(subtractor_1_out), .eq(comparator_1_eq));  // open: gt, lt
  Clock clock_2 (.out(clock_2_out));
  Register #(.width(4)) register_2 (.D(fab_1_out_1), .en(multiplexer_1_out), .Q(Nth), .clk(clock_3_out));  // open: clr
  Clock clock_3 (.out(clock_3_out));
  Register #(.width(1)) register_3 (.D(1'b1), .en(comparator_1_eq), .Q(register_3_q), .clk(clock_2_out));  // open: clr
  Multiplexer multiplexer_1 (
    .in0(comparator_1_eq), .in1(1'b0), .out(multiplexer_1_out), .sel(register_3_q));  // open: en
endmodule

module Fab (
  output [3:0] out_1
);

  wire clock_1_out, clock_2_out, clock_3_out, register_1_q;
  wire [3:0] multiplexer_1_out, register_2_q, register_3_q;

  Register #(.width(1)) register_1 (.D(1'b1), .en(1'b1), .Q(register_1_q), .clk(clock_1_out));  // open: clr
  Clock clock_1 (.out(clock_1_out));
  Multiplexer #(.width(4)) multiplexer_1 (
    .in0(4'b0001), .in1(register_3_q), .out(multiplexer_1_out), .sel(register_1_q));  // open: en
  Adder #(.width(4)) adder_1 (.a(multiplexer_1_out), .b(register_2_q), .out(out_1));  // open: cin, cout
  Register #(.width(4)) register_2 (.D(out_1), .en(1'b1), .Q(register_2_q), .clk(clock_2_out));  // open: clr
  Clock clock_2 (.out(clock_2_out));
  Clock clock_3 (.out(clock_3_out));
  Register #(.width(4)) register_3 (.D(register_2_q), .en(1'b1), .Q(register_3_q), .clk(clock_3_out));  // open: clr
endmodule
